// Logisim project CPU.circ as structural Verilog: 22 circuits, main circuit PC
module PC (
  input  HALT,
  input  RESUME,
  input  RESET,
  input  [31:0] in_4,
  input  [3:0] in_5
);

  wire and_1_out, and_2_out, and_3_out, and_4_out, buffer_1_out_2, cpu_1_out_5, cpu_1_out_8, cpu_1_out_9,
       cpu_1_out_10, cpu_1_out_13, cpu_1_out_14, d_ff_1_q, keyboard_1_avail, keyboard_3_out_5, nor_1_out,
       not_1_out, not_2_out, not_3_out, not_4_out, not_5_out, or_1_out, ram_1_raise_error, undriven;
  wire [3:0] cpu_1_out_7, cpu_1_out_16, number_display_1_out_3, number_display_1_out_4,
       number_display_1_out_5, number_display_1_out_6, number_display_1_out_7, number_display_1_out_8,
       number_display_1_out_9, number_display_1_out_10;
  wire [6:0] keyboard_1_data, keyboard_2_data;
  wire [11:0] counter_1_q;
  wire [15:0] cpu_1_out_6, cpu_1_out_6_2;

  // Probe on undriven
  Keyboard keyboard_1 (.clk(buffer_1_out_2), .avail(keyboard_1_avail), .data(keyboard_1_data));  // open: re, clr
  nor nor_1 (nor_1_out, ~keyboard_1_avail, buffer_1_out_2);  // NOR_Gate
  buffer buffer_1 (.in_1(nor_1_out), .out_2(buffer_1_out_2));
  or or_1 (or_1_out, HALT, ram_1_raise_error);
  CPU cpu_1 (
    .in_1({cpu_1_out_6_2, cpu_1_out_6}), .in_2(or_1_out), .in_3(RESUME), .in_4(RESET),
    .out_6({cpu_1_out_6_2, cpu_1_out_6}), .out_15(cpu_1_out_16[1]), .out_16(cpu_1_out_16[0]),
    .out_5(cpu_1_out_5), .out_11(cpu_1_out_16[2]), .out_12(cpu_1_out_16[3]), .out_13(cpu_1_out_13),
    .out_14(cpu_1_out_14), .out_7(cpu_1_out_7), .out_8(cpu_1_out_8), .out_9(cpu_1_out_9),
    .out_10(cpu_1_out_10));
  // Probe on cpu_1_out_16
  RAM ram_1 (
    .in_3(cpu_1_out_9), .in_6(cpu_1_out_8), .in_4({cpu_1_out_6_2, cpu_1_out_6}), .in_5(cpu_1_out_5),
    .in_2(cpu_1_out_7), .in_1(cpu_1_out_10), .in_7(cpu_1_out_13), .in_8(cpu_1_out_14),
    .out_9({cpu_1_out_6_2, cpu_1_out_6}), .RAISE_ERROR(ram_1_raise_error));
  not not_1 (not_1_out, cpu_1_out_6[0]);
  not not_2 (not_2_out, cpu_1_out_6[1]);
  not not_3 (not_3_out, cpu_1_out_6[5]);
  not not_4 (not_4_out, cpu_1_out_6[7]);
  Keyboard keyboard_2 (.clk(keyboard_3_out_5), .data(keyboard_2_data));  // open: re, clr, avail
  NUMBER_DISPLAY number_display_1 (
    .in_1({cpu_1_out_6_2, cpu_1_out_6}), .in_2(cpu_1_out_16), .out_6(number_display_1_out_6),
    .out_7(number_display_1_out_7), .out_8(number_display_1_out_8), .out_9(number_display_1_out_9),
    .out_10(number_display_1_out_10), .out_3(number_display_1_out_3), .out_4(number_display_1_out_4),
    .out_5(number_display_1_out_5));
  Hex_Digit_Display hex_digit_display_1 (.value(number_display_1_out_3));  // open: dp
  TTY tty_1 (.data(keyboard_1_data), .clk(buffer_1_out_2));  // open: we, clr
  TTY #(.cols(64)) tty_2 (.data(cpu_1_out_6[6:0]), .clk(and_4_out));  // open: we, clr
  and and_1 (and_1_out, 1'b1, not_1_out, not_2_out, cpu_1_out_6[2], cpu_1_out_6[3], cpu_1_out_6[4], not_3_out, cpu_1_out_6[6], not_4_out);
  not not_5 (not_5_out, cpu_1_out_16[2]);
  KEYBOARD keyboard_3 (
    .in_2({cpu_1_out_6_2, cpu_1_out_6}), .in_3(cpu_1_out_16), .in_1(keyboard_2_data),
    .out_4({cpu_1_out_6_2, cpu_1_out_6}), .out_5(keyboard_3_out_5));
  Hex_Digit_Display hex_digit_display_2 (.value(number_display_1_out_4));  // open: dp
  Hex_Digit_Display hex_digit_display_3 (.value(number_display_1_out_5));  // open: dp
  D_Flip_Flop d_ff_1 (.clk(and_2_out), .D(and_1_out), .Q(d_ff_1_q));  // open: Qn, preset, reset
  and and_2 (and_2_out, cpu_1_out_16[0], cpu_1_out_16[2], cpu_1_out_16[3]);
  and and_3 (and_3_out, cpu_1_out_16[0], cpu_1_out_16[3], not_5_out);
  Hex_Digit_Display hex_digit_display_4 (.value(number_display_1_out_6));  // open: dp
  Hex_Digit_Display hex_digit_display_5 (.value(number_display_1_out_7));  // open: dp
  Counter #(.max('hfff), .width(12)) counter_1 (
    .Q(counter_1_q), .clk(and_4_out));  // open: load, D, count, carry, up, clr
  and and_4 (and_4_out, d_ff_1_q, and_3_out);
  Hex_Digit_Display hex_digit_display_6 (.value(number_display_1_out_8));  // open: dp
  Hex_Digit_Display hex_digit_display_7 (.value(number_display_1_out_9));  // open: dp
  RAM_part #(.addrWidth(12), .dataWidth(7), .enables("line")) ram_2 (
    .addr(counter_1_q), .we(1'b1), .clk(and_4_out), .din(cpu_1_out_6[6:0]));  // open: dout
  Hex_Digit_Display hex_digit_display_8 (.value(number_display_1_out_10));  // open: dp

  // Notes on the sheet:
  //   CLOCK S
  //   CLK E
  //   D/A
  //   I/O
endmodule

module CPU (
  input  [31:0] in_1,
  input  in_2,
  input  in_3,
  input  in_4,
  output out_5,
  output [31:0] out_6,
  output [3:0] out_7,
  output out_8,
  output out_9,
  output out_10,
  output out_11,
  output out_12,
  output out_13,
  output out_14,
  output out_15,
  output out_16
);

  wire alu_1_out_5, alu_1_out_6, alu_1_out_7, alu_1_out_8, alu_1_out_9, clock_1_out, control_section_1_acc,
       control_section_1_acc_s, control_section_1_bus_1_bfd35e32, control_section_1_flag,
       control_section_1_iar, control_section_1_iar_136508e1, control_section_1_iar_e, control_section_1_in,
       control_section_1_ir, control_section_1_out, control_section_1_out_13, control_section_1_tmp,
       flag_reg_1_out_6, flag_reg_1_out_7, flag_reg_1_out_8, flag_reg_1_out_9;
  wire [5:0] control_section_1_out_34;
  wire [15:0] control_section_1_out_31, control_section_1_out_32, intruction_register_1_out_3;
  wire [31:0] alu_1_out_10, controlled_buffer_2_out, tmp_1_out_4;

  assign out_6 = control_section_1_out ? controlled_buffer_2_out : 32'bz;  // Controlled_Buffer controlled_buffer_1
  assign controlled_buffer_2_out = control_section_1_in ? in_1 : 32'bz;  // Controlled_Buffer controlled_buffer_2
  TMP tmp_1 (
    .in_1(controlled_buffer_2_out), .in_3(control_section_1_bus_1_bfd35e32), .in_2(control_section_1_tmp),
    .out_4(tmp_1_out_4));
  ALU alu_1 (
    .A(controlled_buffer_2_out), .B(tmp_1_out_4), .in_4(control_section_1_out_34), .out_10(alu_1_out_10),
    .out_6(alu_1_out_6), .out_7(alu_1_out_7), .out_8(alu_1_out_8), .out_9(alu_1_out_9), .out_5(alu_1_out_5));  // open: in_3
  ACC acc_1 (
    .in_1(alu_1_out_10), .in_2(control_section_1_acc_s), .in_3(control_section_1_acc),
    .out_4(controlled_buffer_2_out));
  Clock clock_1 (.out(clock_1_out));
  FLAG_REG flag_reg_1 (
    .in_1(alu_1_out_9), .in_2(alu_1_out_6), .in_3(alu_1_out_7), .in_4(alu_1_out_8),
    .in_5(control_section_1_flag), .out_6(flag_reg_1_out_6), .out_7(flag_reg_1_out_7),
    .out_8(flag_reg_1_out_8), .out_9(flag_reg_1_out_9));
  CPU_REG cpu_reg_1 (
    .in_1(controlled_buffer_2_out), .in_2(control_section_1_out_31), .in_3(control_section_1_out_32),
    .out_4(controlled_buffer_2_out));
  CONTROL_SECTION control_section_1 (
    .in_10(intruction_register_1_out_3), .in_6(flag_reg_1_out_6), .in_7(flag_reg_1_out_7),
    .in_8(flag_reg_1_out_8), .in_9(flag_reg_1_out_9), .BREAK(alu_1_out_5), .CLK(clock_1_out), .HALT(in_2),
    .RESET(in_4), .RESUME(in_3), .out_13(control_section_1_out_13), .out(control_section_1_out),
    .DATA_ADDRESS_6059bfda(out_11), .INPUT_OUTPUT_5ddf5234(out_12), .in(control_section_1_in),
    .RAM_S(out_13), .MAR(out_5), .IAR(control_section_1_iar), .IAR_136508e1(control_section_1_iar_136508e1),
    .IR(control_section_1_ir), .ACC_S(control_section_1_acc_s), .TMP(control_section_1_tmp),
    .I_O_CLK_S(out_16), .FLAG(control_section_1_flag), .STACK_S(out_8), .STACK_OP_a5e0941b(out_7),
    .out_31(control_section_1_out_31), .out_32(control_section_1_out_32),
    .bus_1_bfd35e32(control_section_1_bus_1_bfd35e32), .ACC(control_section_1_acc),
    .IAR_E(control_section_1_iar_e), .STACK_E(out_9), .ARR_E(out_10), .I_O_CLK_E(out_15), .RAM(out_14),
    .out_34(control_section_1_out_34));
  INTRUCTION_REGISTER intruction_register_1 (
    .in_1(controlled_buffer_2_out), .in_2(control_section_1_ir), .out_3(intruction_register_1_out_3));
  IAR iar_1 (
    .enable(control_section_1_iar_e), .clock(control_section_1_iar_136508e1),
    .reset(control_section_1_out_13), .set(control_section_1_iar), .in_5(controlled_buffer_2_out),
    .out_6(controlled_buffer_2_out));

  // Notes on the sheet:
  //   FPU
endmodule

module CONTROL_SECTION (
  input  CLK,
  input  HALT,
  input  RESET,
  input  RESUME,
  input  BREAK,
  input  in_6,
  input  in_7,
  input  in_8,
  input  in_9,
  input  [15:0] in_10,
  output in,
  output out,
  output out_13,
  output RAM_S,
  output bus_1_bfd35e32,
  output MAR,
  output ACC,
  output IAR,
  output IAR_136508e1,
  output IAR_E,
  output IR,
  output STACK_E,
  output ARR_E,
  output I_O_CLK_E,
  output ACC_S,
  output TMP,
  output I_O_CLK_S,
  output FLAG,
  output RAM,
  output STACK_S,
  output [15:0] out_31,
  output [15:0] out_32,
  output [3:0] STACK_OP_a5e0941b,
  output [5:0] out_34,
  output DATA_ADDRESS_6059bfda,
  output INPUT_OUTPUT_5ddf5234
);

  wire A_out, and_1_out, and_2_out, and_11_out, and_12_out, and_13_out, and_18_out, and_19_out, and_20_out,
       and_21_out, and_22_out, and_23_out, and_24_out, and_25_out, and_26_out, and_27_out, and_28_out,
       and_29_out, and_30_out, and_31_out, and_32_out, and_33_out, and_34_out, and_35_out, and_36_out,
       and_37_out, and_38_out, and_39_out, and_40_out, and_41_out, and_42_out, and_43_out, and_44_out,
       and_45_out, and_46_out, and_47_out, and_48_out, and_49_out, and_50_out, and_51_out, and_52_out,
       and_53_out, and_54_out, and_55_out, and_56_out, and_57_out, and_58_out, and_59_out, and_60_out,
       and_61_out, and_62_out, and_63_out, and_64_out, and_65_out, and_66_out, and_67_out, and_68_out,
       and_69_out, and_70_out, and_71_out, and_72_out, and_73_out, and_74_out, and_75_out, and_76_out,
       and_77_out, and_78_out, and_79_out, and_80_out, and_81_out, and_82_out, and_83_out, and_84_out,
       and_85_out, and_96_out, BREAK_t, break_t_t, C_out, clock_1_out_2, clock_1_out_3, clock_1_out_4,
       d_ff_1_q, decoder_3_out0, decoder_3_out1, decoder_3_out2, decoder_3_out3, decoder_3_out4,
       decoder_3_out5, decoder_3_out6, decoder_3_out7, decoder_3_out8, decoder_3_out9, decoder_3_out10,
       decoder_3_out11, decoder_3_out12, decoder_3_out13, decoder_3_out14, decoder_3_out15, decoder_4_out0,
       decoder_4_out1, decoder_4_out2, decoder_4_out3, decoder_4_out4, decoder_4_out5, demultiplexer_1_out2,
       demultiplexer_2_out0, demultiplexer_2_out1, demultiplexer_2_out2, demultiplexer_2_out3,
       demultiplexer_2_out4, demultiplexer_2_out5, demultiplexer_3_out0, demultiplexer_3_out1,
       demultiplexer_3_out2, demultiplexer_3_out3, demultiplexer_3_out4, N_out, nand_1_out, nor_1_out,
       not_1_out, not_2_out, not_3_out, not_4_out, not_5_out, not_6_out, not_7_out, not_8_out, not_9_out,
       not_10_out, not_11_out, not_12_out, not_13_out, not_14_out, or_1_out, or_3_out, or_4_out, or_5_out,
       or_6_out, or_7_out, or_8_out, or_9_out, or_10_out, or_11_out, or_13_out, or_14_out, or_15_out,
       or_16_out, or_17_out, or_18_out, or_19_out, or_20_out, or_21_out, or_22_out, or_24_out, or_25_out,
       or_26_out, or_27_out, or_28_out, or_29_out, or_30_out, or_31_out, or_32_out, or_34_out, or_35_out,
       or_36_out, or_37_out, or_38_out, or_39_out, or_40_out, or_41_out, or_42_out, or_43_out, R0_out,
       stepper_1_out_3, Z_out;
  wire [3:0] stepper_1_out_4;
  wire [14:0] pull_resistor_6_node;
  wire [15:0] decoder_1_out0, decoder_2_out0, decoder_5_out0, or_2_out, pull_resistor_3_node,
       pull_resistor_4_node, pull_resistor_5_node;
  wire [15:1] pull_resistor_2_node;

  not not_1 (not_1_out, CLK);
  or or_1 (or_1_out, HALT, d_ff_1_q, RESET);
  not not_2 (not_2_out, BREAK);
  Pull_Resistor pull_resistor_1 (.node(BREAK_t));
  and and_1 (and_1_out, not_1_out, not_2_out);
  nand nand_1 (nand_1_out, or_1_out, decoder_4_out0);
  and and_2 (and_2_out, and_1_out, nand_1_out);
  not not_3 (not_3_out, and_2_out);
  and and_3 (out_13, nand_1_out, RESET);
  CLOCK clock_1 (.in_1(not_3_out), .out_2(clock_1_out_2), .out_3(clock_1_out_3), .out_4(clock_1_out_4));
  and and_4 (bus_1_bfd35e32, clock_1_out_4, and_36_out);
  and and_5 (ACC, clock_1_out_4, or_8_out);
  and and_6 (IAR_E, clock_1_out_4, or_3_out);
  and and_7 (STACK_E, clock_1_out_4, or_4_out);
  and and_8 (ARR_E, clock_1_out_4, or_22_out);
  and and_9 (I_O_CLK_E, clock_1_out_4, and_62_out);
  and and_10 (RAM, or_7_out, clock_1_out_4);
  and and_11 (and_11_out, or_27_out, clock_1_out_4);
  assign or_2_out = pull_resistor_3_node | pull_resistor_4_node;  // OR_Gate or_2, 16 bits wide
  Multiplexer #(.width(16)) multiplexer_1 (
    .in0(or_2_out), .in1({pull_resistor_2_node, 1'b1}), .out(out_32), .sel(and_11_out));
  Pull_Resistor pull_resistor_2 (.node(pull_resistor_2_node));
  or or_3 (or_3_out, or_9_out, and_28_out, and_39_out, or_15_out);
  or or_4 (or_4_out, and_72_out, demultiplexer_1_out2, and_43_out);
  and and_12 (and_12_out, clock_1_out_4, or_5_out);
  Pull_Resistor pull_resistor_3 (.node(pull_resistor_3_node));
  assign pull_resistor_3_node = and_12_out ? decoder_1_out0 : 16'bz;  // Controlled_Buffer controlled_buffer_1
  and and_13 (and_13_out, clock_1_out_4, or_6_out);
  Pull_Resistor pull_resistor_4 (.node(pull_resistor_4_node));
  assign pull_resistor_4_node = and_13_out ? decoder_2_out0 : 16'bz;  // Controlled_Buffer controlled_buffer_2
  D_Flip_Flop d_ff_1 (.Q(d_ff_1_q), .preset(and_51_out), .reset(RESUME));  // open: clk, D, Qn
  or or_5 (or_5_out, and_57_out, or_28_out, and_41_out, and_22_out, and_53_out, or_22_out);
  or or_6 (or_6_out, and_24_out, and_26_out, and_47_out, or_21_out, and_45_out, and_49_out);
  or or_7 (or_7_out, and_58_out, decoder_4_out1, and_56_out, or_18_out, and_54_out, and_82_out);
  Decoder #(.enable("false"), .select(4)) decoder_1 (
    .out0(decoder_1_out0[0]), .out1(decoder_1_out0[1]), .out2(decoder_1_out0[2]), .out3(decoder_1_out0[3]),
    .out4(decoder_1_out0[4]), .out5(decoder_1_out0[5]), .out6(decoder_1_out0[6]), .out7(decoder_1_out0[7]),
    .out8(decoder_1_out0[8]), .out9(decoder_1_out0[9]), .out10(decoder_1_out0[10]),
    .out11(decoder_1_out0[11]), .out12(decoder_1_out0[12]), .out13(decoder_1_out0[13]),
    .out14(decoder_1_out0[14]), .out15(decoder_1_out0[15]), .sel(in_10[3:0]));
  Decoder #(.enable("false"), .select(4)) decoder_2 (
    .out0(decoder_2_out0[0]), .out1(decoder_2_out0[1]), .out2(decoder_2_out0[2]), .out3(decoder_2_out0[3]),
    .out4(decoder_2_out0[4]), .out5(decoder_2_out0[5]), .out6(decoder_2_out0[6]), .out7(decoder_2_out0[7]),
    .out8(decoder_2_out0[8]), .out9(decoder_2_out0[9]), .out10(decoder_2_out0[10]),
    .out11(decoder_2_out0[11]), .out12(decoder_2_out0[12]), .out13(decoder_2_out0[13]),
    .out14(decoder_2_out0[14]), .out15(decoder_2_out0[15]), .sel(in_10[7:4]));
  stepper stepper_1 (.in_1(clock_1_out_3), .in_2(or_14_out), .out_3(stepper_1_out_3), .out_4(stepper_1_out_4));
  or or_8 (or_8_out, or_26_out, or_25_out);
  Decoder #(.enable("false"), .select(4)) decoder_3 (
    .out0(decoder_3_out0), .out1(decoder_3_out1), .out2(decoder_3_out2), .out3(decoder_3_out3),
    .out4(decoder_3_out4), .out5(decoder_3_out5), .out6(decoder_3_out6), .out7(decoder_3_out7),
    .out8(decoder_3_out8), .out9(decoder_3_out9), .out10(decoder_3_out10), .out11(decoder_3_out11),
    .out12(decoder_3_out12), .out13(decoder_3_out13), .out14(decoder_3_out14), .out15(decoder_3_out15),
    .sel(in_10[11:8]));
  and and_14 (out_34[0], or_11_out, in_10[8], or_10_out);
  and and_15 (out_34[1], or_11_out, in_10[9], or_10_out);
  and and_16 (out_34[2], or_11_out, in_10[10], or_10_out);
  and and_17 (out_34[3], or_11_out, in_10[11], or_10_out);
  or or_9 (or_9_out, decoder_4_out0, and_20_out);
  not not_4 (not_4_out, in_10[14]);
  or or_10 (or_10_out, decoder_4_out3, and_73_out);
  or or_11 (or_11_out, in_10[12], in_10[14]);
  or or_12 (out_34[5], or_11_out, or_18_out);
  not not_5 (not_5_out, not_6_out);
  not not_6 (not_6_out, or_11_out);
  Decoder #(.select(4)) decoder_4 (
    .out0(decoder_4_out0), .out1(decoder_4_out1), .out2(decoder_4_out2), .out3(decoder_4_out3),
    .out4(decoder_4_out4), .out5(decoder_4_out5), .sel(stepper_1_out_4), .en(stepper_1_out_3));  // open: out6, out7, out8, out9, out10, out11, out12, out13, out14, out15
  or or_13 (or_13_out, decoder_4_out1, and_54_out);
  and and_18 (and_18_out, decoder_4_out2, and_19_out);
  and and_19 (and_19_out, decoder_3_out0, not_6_out);
  and and_20 (and_20_out, decoder_4_out2, and_21_out);
  and and_21 (and_21_out, not_5_out, in_10[14]);
  and and_22 (and_22_out, decoder_4_out2, and_23_out);
  and and_23 (and_23_out, not_4_out, not_5_out);
  and and_24 (and_24_out, decoder_4_out2, and_25_out);
  and and_25 (and_25_out, not_6_out, decoder_3_out1);
  and and_26 (and_26_out, decoder_4_out2, and_27_out);
  and and_27 (and_27_out, not_6_out, decoder_3_out2);
  and and_28 (and_28_out, decoder_4_out2, and_29_out);
  and and_29 (and_29_out, not_6_out, decoder_3_out3);
  and and_30 (and_30_out, decoder_4_out2, and_31_out);
  and and_31 (and_31_out, not_6_out, decoder_3_out4);
  and and_32 (and_32_out, decoder_4_out2, and_33_out);
  and and_33 (and_33_out, not_6_out, decoder_3_out5);
  and and_34 (and_34_out, decoder_4_out2, and_35_out);
  and and_35 (and_35_out, not_6_out, decoder_3_out6);
  and and_36 (and_36_out, decoder_4_out2, and_37_out);
  and and_37 (and_37_out, not_6_out, decoder_3_out7);
  and and_38 (and_38_out, not_6_out, decoder_3_out8);
  and and_39 (and_39_out, decoder_4_out2, and_40_out);
  and and_40 (and_40_out, not_6_out, decoder_3_out9);
  and and_41 (and_41_out, decoder_4_out2, and_42_out);
  and and_42 (and_42_out, not_6_out, decoder_3_out10);
  and and_43 (and_43_out, decoder_4_out2, and_44_out);
  and and_44 (and_44_out, not_6_out, decoder_3_out11);
  and and_45 (and_45_out, decoder_4_out2, and_46_out);
  and and_46 (and_46_out, not_6_out, decoder_3_out12);
  and and_47 (and_47_out, decoder_4_out2, and_48_out);
  and and_48 (and_48_out, not_6_out, decoder_3_out13);
  and and_49 (and_49_out, decoder_4_out2, and_50_out);
  and and_50 (and_50_out, not_6_out, decoder_3_out14);
  and and_51 (and_51_out, decoder_4_out2, and_52_out);
  and and_52 (and_52_out, not_6_out, decoder_3_out15);
  or or_14 (or_14_out, or_24_out, or_17_out, or_16_out, and_51_out, and_49_out);
  or or_15 (or_15_out, and_30_out, and_32_out, and_34_out);
  and and_53 (and_53_out, decoder_4_out2, in_10[5], and_38_out);
  not not_7 (not_7_out, in_6);
  not not_8 (not_8_out, in_7);
  not not_9 (not_9_out, in_8);
  not not_10 (not_10_out, in_9);
  or or_16 (or_16_out, and_36_out, and_41_out, and_39_out, and_53_out);
  and and_54 (and_54_out, decoder_4_out3, and_21_out);
  and and_55 (and_55_out, decoder_4_out3, and_23_out);
  and and_56 (and_56_out, decoder_4_out3, and_25_out);
  and and_57 (and_57_out, decoder_4_out3, and_27_out);
  and and_58 (and_58_out, decoder_4_out3, and_29_out);
  and and_59 (and_59_out, decoder_4_out3, and_31_out);
  and and_60 (and_60_out, decoder_4_out3, and_33_out);
  and and_61 (and_61_out, decoder_4_out3, and_35_out);
  and and_62 (and_62_out, decoder_4_out3, not_11_out, and_38_out);
  not not_11 (not_11_out, in_10[5]);
  and and_63 (and_63_out, decoder_4_out3, and_44_out);
  and and_64 (and_64_out, decoder_4_out3, and_46_out);
  and and_65 (and_65_out, decoder_4_out3, and_48_out);
  and C (C_out, in_10[3], in_6);
  and A (A_out, in_10[2], in_7);
  and and_66 (and_66_out, in_10[1], in_8);
  and and_67 (and_67_out, in_10[0], in_9);
  and and_68 (and_68_out, in_10[3], not_7_out);
  and and_69 (and_69_out, in_10[2], not_8_out);
  and N (N_out, in_10[1], not_9_out);
  and Z (Z_out, in_10[0], not_10_out);
  and and_70 (and_70_out, in_10[8], in_10[9], in_10[10], in_10[11]);
  not not_12 (not_12_out, and_70_out);
  or or_17 (or_17_out, and_57_out, and_18_out, and_62_out, and_56_out, and_71_out);
  and and_71 (and_71_out, and_72_out, not_13_out);
  or or_18 (or_18_out, and_59_out, and_60_out, and_61_out);
  and and_72 (and_72_out, and_63_out, not_14_out);
  or or_19 (or_19_out, C_out, A_out, and_66_out, and_67_out);
  or or_20 (or_20_out, and_68_out, and_69_out, N_out, Z_out);
  or or_21 (or_21_out, and_55_out, and_73_out);
  or or_22 (or_22_out, and_64_out, and_65_out);
  Demultiplexer #(.select(3)) demultiplexer_1 (
    .out2(demultiplexer_1_out2), .in(and_81_out), .sel(in_10[6:4]));  // open: out0, out1, out3, out4, out5, out6, out7
  Demultiplexer #(.select(3)) demultiplexer_2 (
    .out0(demultiplexer_2_out0), .out1(demultiplexer_2_out1), .out2(demultiplexer_2_out2),
    .out3(demultiplexer_2_out3), .out4(demultiplexer_2_out4), .out5(demultiplexer_2_out5), .in(and_63_out),
    .sel(in_10[6:4]));  // open: out6, out7
  Demultiplexer #(.select(3)) demultiplexer_3 (
    .out0(demultiplexer_3_out0), .out1(demultiplexer_3_out1), .out2(demultiplexer_3_out2),
    .out3(demultiplexer_3_out3), .out4(demultiplexer_3_out4), .out5(break_t_t), .in(and_43_out),
    .sel(in_10[6:4]));  // open: out6, out7
  or or_23 (out, or_22_out, or_29_out, or_27_out, or_28_out, and_53_out);
  or or_24 (or_24_out, or_25_out, and_81_out, and_75_out, or_32_out, or_30_out, and_82_out, or_27_out);
  or or_25 (or_25_out, and_74_out, and_85_out);
  and and_73 (and_73_out, decoder_4_out4, and_21_out);
  and and_74 (and_74_out, decoder_4_out4, and_23_out, not_12_out);
  and and_75 (and_75_out, decoder_4_out4, and_29_out);
  and and_76 (and_76_out, decoder_4_out4, and_31_out);
  and and_77 (and_77_out, decoder_4_out4, or_19_out, and_33_out);
  or or_26 (or_26_out, and_76_out, and_77_out, and_78_out);
  and and_78 (and_78_out, decoder_4_out4, or_20_out, and_35_out);
  and and_79 (and_79_out, decoder_4_out4, and_33_out);
  and and_80 (and_80_out, decoder_4_out4, and_35_out);
  not not_13 (not_13_out, demultiplexer_2_out2);
  not not_14 (not_14_out, or_27_out);
  and and_81 (and_81_out, decoder_4_out4, and_44_out);
  and and_82 (and_82_out, decoder_4_out4, and_46_out);
  and and_83 (and_83_out, decoder_4_out4, and_48_out);
  or or_27 (or_27_out, and_83_out, demultiplexer_2_out4);
  or or_28 (or_28_out, demultiplexer_3_out0, demultiplexer_3_out4, break_t_t);
  or or_29 (or_29_out, or_9_out, and_24_out, and_26_out, and_28_out, or_15_out, and_45_out, and_47_out);
  or or_30 (or_30_out, demultiplexer_2_out0, or_31_out, demultiplexer_2_out3);
  or or_31 (or_31_out, demultiplexer_2_out1, demultiplexer_2_out5);
  and and_84 (and_84_out, nor_1_out, or_41_out);
  nor nor_1 (nor_1_out, and_39_out, and_49_out);
  and and_85 (and_85_out, decoder_4_out5, and_21_out);
  or or_32 (or_32_out, and_76_out, and_79_out, and_80_out);
  Decoder #(.enable("false"), .select(4)) decoder_5 (
    .out0(decoder_5_out0[0]), .out1(decoder_5_out0[1]), .out2(decoder_5_out0[2]), .out3(decoder_5_out0[3]),
    .out4(decoder_5_out0[4]), .out5(decoder_5_out0[5]), .out6(decoder_5_out0[6]), .out7(decoder_5_out0[7]),
    .out8(decoder_5_out0[8]), .out9(decoder_5_out0[9]), .out10(decoder_5_out0[10]),
    .out11(decoder_5_out0[11]), .out12(decoder_5_out0[12]), .out13(decoder_5_out0[13]),
    .out14(decoder_5_out0[14]), .out15(decoder_5_out0[15]), .sel(in_10[3:0]));
  or or_33 (in, or_18_out, and_54_out, and_84_out, or_35_out, decoder_4_out1);
  or or_34 (or_34_out, and_57_out, or_27_out);
  or or_35 (or_35_out, and_82_out, or_36_out);
  or or_36 (or_36_out, or_26_out, and_41_out);
  or or_37 (or_37_out, or_13_out, and_75_out, or_18_out);
  or or_38 (or_38_out, or_21_out, or_18_out);
  or or_39 (or_39_out, and_54_out, or_15_out, and_22_out);
  or or_40 (or_40_out, and_36_out, or_21_out);
  or or_41 (or_41_out, and_49_out, and_39_out, and_58_out, and_56_out, and_62_out, or_31_out);
  or or_42 (or_42_out, and_43_out, and_72_out, demultiplexer_1_out2, or_22_out, and_65_out);
  or or_43 (or_43_out, and_82_out, or_25_out, demultiplexer_2_out5);
  or or_44 (STACK_OP_a5e0941b[0], demultiplexer_2_out1, demultiplexer_3_out1, demultiplexer_2_out5, demultiplexer_3_out2, demultiplexer_3_out3);
  or or_45 (STACK_OP_a5e0941b[1], demultiplexer_2_out2, demultiplexer_3_out0, demultiplexer_3_out2, demultiplexer_3_out3);
  or or_46 (STACK_OP_a5e0941b[2], demultiplexer_1_out2, demultiplexer_2_out0, demultiplexer_2_out2, demultiplexer_3_out1, demultiplexer_3_out3);
  or or_47 (STACK_OP_a5e0941b[3], demultiplexer_3_out4, demultiplexer_2_out1, break_t_t);
  and and_86 (RAM_S, clock_1_out_2, or_34_out);
  and and_87 (MAR, clock_1_out_2, or_29_out);
  and and_88 (IAR, clock_1_out_2, or_36_out);
  and and_89 (IAR_136508e1, clock_1_out_2, or_37_out);
  and and_90 (IR, clock_1_out_2, decoder_4_out1);
  and and_91 (ACC_S, clock_1_out_2, or_38_out);
  and and_92 (TMP, clock_1_out_2, or_39_out);
  and and_93 (I_O_CLK_S, and_53_out, clock_1_out_2);
  and and_94 (FLAG, clock_1_out_2, or_40_out);
  and and_95 (STACK_S, clock_1_out_2, or_42_out);
  and and_96 (and_96_out, clock_1_out_2, or_41_out);
  and R0 (R0_out, clock_1_out_2, or_43_out);
  Pull_Resistor pull_resistor_5 (.node(pull_resistor_5_node));
  assign pull_resistor_5_node = and_96_out ? decoder_5_out0 : 16'bz;  // Controlled_Buffer controlled_buffer_3
  Pull_Resistor pull_resistor_6 (.node(pull_resistor_6_node));
  Multiplexer #(.width(16)) multiplexer_2 (
    .in0(pull_resistor_5_node), .in1({pull_resistor_6_node, 1'b1}), .out(out_31), .sel(R0_out));

  assign DATA_ADDRESS_6059bfda = in_10[4];
  assign INPUT_OUTPUT_5ddf5234 = in_10[5];
  assign out_34[4] = in_10[13];

  // Notes on the sheet:
  //   reg B
  //   reg A
endmodule

module ROM (
  input  [31:0] in_1,
  input  in_2,
  input  in_3,
  output [31:0] out_4
);

  wire and_1_out, not_1_out;
  wire [16:0] register_1_q;
  wire [31:0] rom_1_data;

  Register #(.width(17)) register_1 (.D(in_1[16:0]), .Q(register_1_q), .clk(in_3));  // open: en, clr
  Pull_Resistor pull_resistor_1 (.node(register_1_q[16]));
  not not_1 (not_1_out, register_1_q[16]);
  ROM_part #(.addrWidth(16), .dataWidth(32)) rom_1 (.addr(register_1_q[15:0]), .data(rom_1_data));
  and and_1 (and_1_out, not_1_out, in_2);
  assign out_4 = and_1_out ? rom_1_data : 32'bz;  // Controlled_Buffer controlled_buffer_1

  // Notes on the sheet:
  //   contents of rom_1 (hex, n*v repeats v):
  //   400 1 302 5c 832 301 16 302 0 c12 1e00 501 6 820 1b02 e02 400 fffffff8 303 14000 232 f00 48 65 6c 6c
  //   6f 2c 20 77 6f 72 6c 64 21 a
endmodule

module RAM (
  input  in_1,
  input  [3:0] in_2,
  input  in_3,
  input  [31:0] in_4,
  input  in_5,
  input  in_6,
  input  in_7,
  input  in_8,
  output [31:0] out_9,
  output RAISE_ERROR
);

  wire and_1_out, and_2_out, and_3_out, and_4_out, and_5_out, and_6_out, and_7_out, demultiplexer_1_out0,
       demultiplexer_1_out1, demultiplexer_1_out2, demultiplexer_1_out3, demultiplexer_1_out4,
       demultiplexer_1_out5, demultiplexer_1_out6, demultiplexer_1_out7, demultiplexer_1_out8,
       demultiplexer_1_out9, nor_1_out, or_1_out, or_2_out, or_3_out, or_4_out, or_5_out, or_6_out, or_7_out,
       or_8_out, or_9_out, or_10_out;
  wire [2:0] adder_1_out_2, controlled_buffer_10_out_2;
  wire [13:0] adder_1_out, controlled_buffer_7_out, controlled_buffer_10_out, controlled_buffer_11_out,
       pull_resistor_3_node, ram_1_dout, register_2_q, register_3_q, subtractor_1_out;
  wire [15:0] controlled_buffer_4_out, register_1_q;
  wire [16:0] controlled_buffer_1_out, pull_resistor_5_node;
  wire [16:16] register_1_q_2;
  wire [31:0] rom_1_data;
  wire [31:14] ram_1_dout_2;

  Demultiplexer #(.select(4)) demultiplexer_1 (
    .out0(demultiplexer_1_out0), .out1(demultiplexer_1_out1), .out2(demultiplexer_1_out2),
    .out3(demultiplexer_1_out3), .out4(demultiplexer_1_out4), .out5(demultiplexer_1_out5),
    .out6(demultiplexer_1_out6), .out7(demultiplexer_1_out7), .out8(demultiplexer_1_out8),
    .out9(demultiplexer_1_out9), .in(in_3), .sel(in_2));  // open: out10, out11, out12, out13, out14, out15
  or or_1 (or_1_out, in_1, demultiplexer_1_out8);
  or or_2 (or_2_out, demultiplexer_1_out1, demultiplexer_1_out9);
  assign controlled_buffer_1_out = or_1_out ? {adder_1_out_2, adder_1_out} : 17'bz;  // Controlled_Buffer controlled_buffer_1
  assign in_4 = demultiplexer_1_out3 ? {{18{1'b0}}, register_2_q} : 32'bz;  // Controlled_Buffer controlled_buffer_2
  assign controlled_buffer_1_out = in_5 ? in_4[16:0] : 17'bz;  // Controlled_Buffer controlled_buffer_3
  and and_1 (and_1_out, or_1_out, in_6);
  Pull_Resistor pull_resistor_1 (.node(in_4));
  or or_3 (or_3_out, demultiplexer_1_out2, demultiplexer_1_out9, demultiplexer_1_out3);
  Register #(.width(17)) register_1 (
    .D(controlled_buffer_1_out), .Q({register_1_q_2[16], register_1_q}), .clk(or_4_out));  // open: en, clr
  or or_4 (or_4_out, and_1_out, in_5);
  assign controlled_buffer_4_out = demultiplexer_1_out0 ? {2'b00, register_2_q} : 16'bz;  // Controlled_Buffer controlled_buffer_4
  assign controlled_buffer_4_out = or_3_out ? {2'b00, register_3_q} : 16'bz;  // Controlled_Buffer controlled_buffer_5
  nor nor_1 (nor_1_out, demultiplexer_1_out0, or_3_out);
  assign controlled_buffer_4_out = nor_1_out ? register_1_q : 16'bz;  // Controlled_Buffer controlled_buffer_6
  Pull_Resistor pull_resistor_2 (.node(register_1_q_2[16]));
  or or_5 (or_5_out, demultiplexer_1_out0, demultiplexer_1_out6);
  assign controlled_buffer_7_out = demultiplexer_1_out7 ? register_2_q : 14'bz;  // Controlled_Buffer controlled_buffer_7
  assign controlled_buffer_7_out = demultiplexer_1_out5 ? subtractor_1_out : 14'bz;  // Controlled_Buffer controlled_buffer_8
  assign controlled_buffer_7_out = demultiplexer_1_out4 ? adder_1_out : 14'bz;  // Controlled_Buffer controlled_buffer_9
  assign {controlled_buffer_10_out_2, controlled_buffer_10_out} = in_1 ? {register_1_q_2[16], register_1_q} : 17'bz;  // Controlled_Buffer controlled_buffer_10
  or or_6 (or_6_out, demultiplexer_1_out2, demultiplexer_1_out3);
  assign controlled_buffer_11_out = demultiplexer_1_out0 ? ram_1_dout : 14'bz;  // Controlled_Buffer controlled_buffer_11
  Register #(.width(14)) register_2 (.D(controlled_buffer_11_out), .Q(register_2_q), .clk(and_2_out));  // open: en, clr
  assign controlled_buffer_11_out = demultiplexer_1_out6 ? register_3_q : 14'bz;  // Controlled_Buffer controlled_buffer_12
  and and_2 (and_2_out, or_5_out, in_6);
  Register #(.width(14)) register_3 (.D(controlled_buffer_7_out), .Q(register_3_q), .clk(and_3_out));  // open: en, clr
  and and_3 (and_3_out, or_7_out, in_6);
  or or_7 (or_7_out, demultiplexer_1_out4, demultiplexer_1_out5, demultiplexer_1_out7);
  RAM_part #(.addrWidth(16), .dataWidth(32), .enables("line")) ram_1 (
    .addr(controlled_buffer_4_out), .we(1'b1), .clk(or_8_out), .din(in_4), .dout({ram_1_dout_2, ram_1_dout}));
  ROM_part #(.addrWidth(16), .dataWidth(32)) rom_1 (.addr(controlled_buffer_4_out), .data(rom_1_data));
  or or_8 (or_8_out, and_4_out, in_7);
  and and_4 (and_4_out, in_6, or_6_out);
  assign controlled_buffer_10_out = demultiplexer_1_out8 ? register_2_q : 14'bz;  // Controlled_Buffer controlled_buffer_13
  Pull_Resistor pull_resistor_3 (.node(pull_resistor_3_node));
  Pull_Resistor pull_resistor_4 (.node(controlled_buffer_10_out_2));
  assign controlled_buffer_10_out = demultiplexer_1_out4 ? register_3_q : 14'bz;  // Controlled_Buffer controlled_buffer_14
  Pull_Resistor pull_resistor_5 (.node(pull_resistor_5_node));
  assign pull_resistor_5_node = or_1_out ? in_4[16:0] : 17'bz;  // Controlled_Buffer controlled_buffer_15
  and and_5 (and_5_out, in_7, ~register_1_q_2[16]);  // AND_Gate
  Subtractor #(.width(14)) subtractor_1 (
    .a(register_3_q), .b(pull_resistor_3_node), .out(subtractor_1_out), .bin(1'b1));  // open: bout
  and and_6 (and_6_out, or_10_out, or_9_out);
  or or_9 (or_9_out, or_2_out, in_8);
  or or_10 (or_10_out, or_2_out, register_1_q_2[16]);
  Adder #(.width(17)) adder_1 (
    .a({controlled_buffer_10_out_2, controlled_buffer_10_out}), .b(pull_resistor_5_node),
    .out({adder_1_out_2, adder_1_out}), .cin(demultiplexer_1_out4));  // open: cout
  and and_7 (and_7_out, ~or_10_out, or_9_out);  // AND_Gate
  Comparator #(.width(17)) comparator_1 (.a({register_1_q_2[16], register_1_q}), .b(17'h287));  // open: gt, eq, lt
  assign out_9 = and_7_out ? rom_1_data : 32'bz;  // Controlled_Buffer controlled_buffer_16
  Pull_Resistor pull_resistor_6 (.node(RAISE_ERROR));
  assign out_9 = and_6_out ? {ram_1_dout_2, ram_1_dout} : 32'bz;  // Controlled_Buffer controlled_buffer_17

  // Notes on the sheet:
  //   contents of rom_1 (hex, n*v repeats v):
  //   400 1 300 11d b00 300 c b00 b20 300 17b a00 e0f b10 ef0 300 14000 b00 300 14 b00 300 1c b00 b20 300
  //   27a a00 e0f b10 b10 ef0 e05 e50 b00 300 124 b00 300 2d b00 b20 300 17b a00 e0f b10 ef0 300 14000 b00
  //   300 3a b00 b20 300 17b a00 e0f b10 ef0 300 128 b00 300 47 b00 b20 300 17b a00 e0f b10 ef0 e0f b10
  //   e05 ef0 e50 b00 300 57 b00 b20 300 193 a00 e0f b10 ef0 300 12b b00 300 64 b00 b20 300 17b a00 e0f
  //   b10 ef0 300 136 b00 300 71 b00 b20 300 17b a00 e0f b10 ef0 300 7b b00 b20 300 2ab a00 5200 2 e05 e50
  //   b00 300 13c b00 300 8a b00 b20 300 17b a00 e0f b10 ef0 e0f b10 e05 ef0 e50 b00 300 9a b00 b20 300
  //   193 a00 e0f b10 ef0 300 a4 b00 b20 300 1b8 a00 300 142 b00 300 ae b00 b20 300 17b a00 e0f b10 ef0
  //   300 b8 b00 b20 300 2cf a00 7300 40000000 e05 e50 b00 300 14a b00 300 c7 b00 b20 300 17b a00 e0f b10
  //   ef0 e0f b10 e05 ef0 e50 b00 300 d7 b00 b20 300 1c4 a00 e0f b10 ef0 300 e1 b00 b20 300 1b8 a00 300
  //   150 b00 300 eb b00 b20 300 17b a00 e0f b10 ef0 300 f5 b00 b20 300 26d a00 e05 e50 b00 300 160 b00
  //   300 102 b00 b20 300 17b a00 e0f b10 ef0 e0f b10 e05 ef0 e50 b00 300 112 b00 b20 300 16e a00 e0f b10
  //   ef0 300 11c b00 b20 300 1b8 a00 f00 6e 61 6d 65 3f 20 0 68 69 20 0 20 28 0 20 6c 65 74 74 65 72 73
  //   29 a 0 69 6e 74 3f 20 0 78 32 20 3d 20 0 66 6c 6f 61 74 3f 20 0 2f 32 20 3d 20 0 70 72 65 73 73 20
  //   61 20 6b 65 79 2e 2e 2e 20 0 79 6f 75 20 70 72 65 73 73 65 64 3a 20 0 301 fffffffe b51 301 5c 831
  //   820 e0f b30 b10 e0e ef0 a0e 301 fffffffe b51 e01 302 5c 832 302 0 c12 1e00 501 6 820 1b02 e02 400
  //   fffffff8 e0f b30 b10 e0e ef0 a0e 301 fffffffe b51 b00 300 14014 b00 300 1a1 b00 b20 300 466 a00 e0f
  //   b10 b10 ef0 300 14014 b00 300 1af b00 b20 300 17b a00 e0f b10 ef0 e0f b30 b10 e0e ef0 a0e 301 5c 831
  //   301 a 821 e0f b30 b10 e0e ef0 a0e 301 fffffffe b51 e01 302 5c 832 1e01 602 6 302 2d 822 3d01 e01
  //   7010 3851b717 e01 e10 b00 e10 b00 300 1e1 b00 b20 300 22f a00 e0f b10 ef0 e0f b10 e01 ef0 e02 3602
  //   e03 3113 e01 e10 b00 e20 b00 300 1f8 b00 b20 300 193 a00 e0f b10 ef0 e0f b10 e01 ef0 302 2e 822 304
  //   4 7210 41200000 e01 e10 b00 e40 b00 e10 b00 300 214 b00 b20 300 22f a00 e0f b10 ef0 e0f b10 e04 b10
  //   e01 ef0 e02 3602 e03 3113 e01 5020 30 820 1c04 e04 601 ffffffdc e0f b30 b10 e0e ef0 a0e 301 fffffffe
  //   b51 3700 e0f b30 b10 e0e ef0 a0e 301 fffffffe b51 e01 302 5c 832 302 30 822 302 78 822 303 8 5710 f
  //   e02 5f20 9 504 5 5020 30 400 3 5020 37 b00 1501 1500 1500 1500 e01 1c03 e03 601 ffffffea 303 8 b10
  //   820 1c03 e03 601 fffffffb e0f b30 b10 e0e ef0 a0e 301 f0 831 800 1e00 501 fffffffd e0f b30 b10 e0e
  //   ef0 a0e 301 fffffffd b51 e01 302 fffffffe b52 1c00 e04 303 0 302 f0 832 805 1e05 501 fffffffd 5f50 a
  //   501 f 5f50 d 501 b 1f34 505 fffffff2 e50 d13 825 1b03 e03 400 ffffffeb 302 a 822 300 0 d13 e30 e0f
  //   b30 b10 e0e ef0 a0e 300 14020 b00 300 20 b00 300 2b8 b00 b20 300 27a a00 e0f b10 b10 ef0 300 14020
  //   b00 300 2c6 b00 b20 300 4a6 a00 e0f b10 ef0 e0f b30 b10 e0e ef0 a0e 300 14020 b00 300 20 b00 300 2dc
  //   b00 b20 300 27a a00 e0f b10 b10 ef0 301 14020 302 0 303 0 304 0 c12 5f00 2d 601 5 304 1 302 1 c12
  //   e06 5f60 2e 501 14 5160 30 502 2a e06 5f60 9 504 25 3606 e06 7230 41200000 3006 e03 1b02 e02 400
  //   ffffffe8 1b02 e02 305 3f800000 c12 5100 30 502 12 e06 5f60 9 504 d 3606 e06 7350 41200000 e05 3265
  //   3003 e03 1b02 e02 400 ffffffeb 1e04 501 8 3d03 e0f b30 b10 e0e ef0 a0e e30 e0f b30 b10 e0e ef0 a0e
  //   301 fffffffe b51 e01 302 0 c12 1e00 501 5 1b02 e02 400 fffffff9 e20 e0f b30 b10 e0e ef0 a0e 301
  //   fffffffd b51 e01 302 fffffffe b52 e02 303 0 c23 d13 1e00 501 5 1b03 e03 400 fffffff8 e30 e0f b30 b10
  //   e0e ef0 a0e 301 fffffffd b51 e01 302 fffffffe b52 e02 303 0 c13 e04 c23 1f04 601 8 1e04 501 d 1b03
  //   e03 400 fffffff4 300 0 e0f b30 b10 e0e ef0 a0e 300 1 e0f b30 b10 e0e ef0 a0e 301 fffffffc b51 e01
  //   302 fffffffd b52 e02 303 fffffffe b53 e03 304 0 1f43 505 7 c24 d14 1b04 e04 400 fffffff8 e0f b30 b10
  //   e0e ef0 a0e 301 fffffffc b51 e01 302 fffffffd b52 e02 303 fffffffe b53 e03 304 0 1f43 505 7 e20 d14
  //   1b04 e04 400 fffffff8 e0f b30 b10 e0e ef0 a0e 301 fffffffe b51 1e00 602 2 1d00 e0f b30 b10 e0e ef0
  //   a0e 301 fffffffd b51 e01 302 ffff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
  //   TRIED WRITING IN ROM
endmodule

module CPU_REG (
  input  [31:0] in_1,
  input  [15:0] in_2,
  input  [15:0] in_3,
  output [31:0] out_4
);

  wire or_1_out;
  wire [31:0] register_1_out_4;

  REGISTER register_1 (.in_1(in_1), .in_2(in_2[0]), .in_3(in_3[0]), .out_4(register_1_out_4));
  REGISTER register_2 (.in_1(in_1), .in_2(in_2[1]), .in_3(in_3[1]), .out_4(register_1_out_4));
  REGISTER register_3 (.in_1(in_1), .in_2(in_2[2]), .in_3(in_3[2]), .out_4(register_1_out_4));
  REGISTER register_4 (.in_1(in_1), .in_2(in_2[3]), .in_3(in_3[3]), .out_4(register_1_out_4));
  REGISTER register_5 (.in_1(in_1), .in_2(in_2[4]), .in_3(in_3[4]), .out_4(register_1_out_4));
  REGISTER register_6 (.in_1(in_1), .in_2(in_2[5]), .in_3(in_3[5]), .out_4(register_1_out_4));
  REGISTER register_7 (.in_1(in_1), .in_2(in_2[6]), .in_3(in_3[6]), .out_4(register_1_out_4));
  REGISTER register_8 (.in_1(in_1), .in_2(in_2[7]), .in_3(in_3[7]), .out_4(register_1_out_4));
  REGISTER register_9 (.in_1(in_1), .in_2(in_2[8]), .in_3(in_3[8]), .out_4(register_1_out_4));
  REGISTER register_10 (.in_1(in_1), .in_2(in_2[9]), .in_3(in_3[9]), .out_4(register_1_out_4));
  REGISTER register_11 (.in_1(in_1), .in_2(in_2[10]), .in_3(in_3[10]), .out_4(register_1_out_4));
  REGISTER register_12 (.in_1(in_1), .in_2(in_2[11]), .in_3(in_3[11]), .out_4(register_1_out_4));
  REGISTER register_13 (.in_1(in_1), .in_2(in_2[12]), .in_3(in_3[12]), .out_4(register_1_out_4));
  REGISTER register_14 (.in_1(in_1), .in_2(in_2[13]), .in_3(in_3[13]), .out_4(register_1_out_4));
  REGISTER register_15 (.in_1(in_1), .in_2(in_2[14]), .in_3(in_3[14]), .out_4(register_1_out_4));
  REGISTER register_16 (.in_1(in_1), .in_2(in_2[15]), .in_3(in_3[15]), .out_4(register_1_out_4));
  assign out_4 = or_1_out ? register_1_out_4 : 32'bz;  // Controlled_Buffer controlled_buffer_1
  or or_1 (or_1_out, in_3[0], in_3[1], in_3[2], in_3[3], in_3[4], in_3[5], in_3[6], in_3[7], in_3[8], in_3[9], in_3[10], in_3[11], in_3[12], in_3[13], in_3[14], in_3[15], 1'b0);
endmodule

module stepper (
  input  in_1,
  input  in_2,
  output out_3,
  output [3:0] out_4
);

  wire and_1_out, and_2_out, d_ff_2_q, not_1_out;

  and and_1 (and_1_out, d_ff_2_q, in_1);
  D_Flip_Flop d_ff_1 (.clk(in_1), .D(1'b1), .Q(out_3), .reset(and_2_out));  // open: Qn, preset
  not not_1 (not_1_out, and_1_out);
  and and_2 (and_2_out, not_1_out, in_2);
  D_Flip_Flop d_ff_2 (.clk(in_1), .D(out_3), .Q(d_ff_2_q), .reset(and_2_out));  // open: Qn, preset
  Counter #(.max('hf), .width(4)) counter_1 (
    .count(1'b1), .Q(out_4), .clk(and_1_out), .clr(and_2_out));  // open: load, D, carry, up
endmodule

module ALU (
  input  [31:0] A,
  input  [31:0] B,
  input  in_3,
  input  [5:0] in_4,
  output out_5,
  output out_6,
  output out_7,
  output out_8,
  output out_9,
  output [31:0] out_10
);

  wire adder_1_cout, and_2_out, and_3_out, and_4_out, and_5_out, bitfinder_1_found, comparator_1_gt,
       decoder_1_out0, decoder_1_out1, decoder_1_out2, decoder_1_out3, decoder_1_out4, decoder_1_out5,
       decoder_1_out6, decoder_1_out7, decoder_1_out8, decoder_1_out9, decoder_1_out10, decoder_1_out11,
       decoder_1_out12, decoder_1_out13, decoder_1_out14, decoder_1_out15, fpu_1_out_6, not_1_out, not_2_out,
       not_4_out, or_1_out, or_4_out, or_5_out, or_6_out, or_7_out, subtractor_1_bout, subtractor_2_bout;
  wire [0:0] or_2_out;
  wire [31:0] adder_1_out, and_1_out, controlled_buffer_1_out, controlled_buffer_2_out, demultiplexer_1_out0,
       demultiplexer_1_out1, demultiplexer_2_out0, demultiplexer_2_out1, divider_1_out, divider_1_rem,
       multiplier_1_out, negator_1_out, not_3_out, or_3_out, pull_resistor_1_node, pull_resistor_3_node,
       subtractor_1_out, subtractor_2_out, xor_1_out;

  assign controlled_buffer_1_out = in_4[5] ? A : 32'bz;  // Controlled_Buffer controlled_buffer_1
  Demultiplexer #(.width(32)) demultiplexer_1 (
    .out0(demultiplexer_1_out0), .out1(demultiplexer_1_out1), .in(controlled_buffer_1_out), .sel(not_2_out));
  assign controlled_buffer_2_out = in_4[5] ? B : 32'bz;  // Controlled_Buffer controlled_buffer_2
  Demultiplexer #(.width(32)) demultiplexer_2 (
    .out0(demultiplexer_2_out0), .out1(demultiplexer_2_out1), .in(controlled_buffer_2_out), .sel(not_2_out));
  Pull_Resistor pull_resistor_1 (.node(pull_resistor_1_node));
  assign pull_resistor_1_node = not_1_out ? demultiplexer_1_out1 : 32'bz;  // Controlled_Buffer controlled_buffer_3
  Pull_Resistor pull_resistor_2 (.node(demultiplexer_2_out1));
  not not_1 (not_1_out, or_1_out);
  or or_1 (or_1_out, decoder_1_out12, decoder_1_out11);
  not not_2 (not_2_out, in_4[4]);
  or or_2 (or_2_out[0], in_3, decoder_1_out11, decoder_1_out12);
  Adder #(.width(32)) adder_1 (
    .a(pull_resistor_1_node), .b(demultiplexer_2_out1), .out(adder_1_out), .cin(or_2_out[0]),
    .cout(adder_1_cout));
  Subtractor #(.width(32)) subtractor_1 (
    .a(pull_resistor_1_node), .b(demultiplexer_2_out1), .out(subtractor_1_out), .bin(or_2_out[0]),
    .bout(subtractor_1_bout));
  Subtractor #(.width(32)) subtractor_2 (
    .a(demultiplexer_2_out1), .b(pull_resistor_3_node), .out(subtractor_2_out), .bin(or_2_out[0]),
    .bout(subtractor_2_bout));
  Pull_Resistor pull_resistor_3 (.node(pull_resistor_3_node));
  Multiplier #(.mode("twosComplement"), .width(32)) multiplier_1 (
    .a(pull_resistor_1_node), .b(demultiplexer_2_out1), .out(multiplier_1_out));  // open: cin, cout
  Divider #(.mode("twosComplement"), .width(32)) divider_1 (
    .a(pull_resistor_1_node), .b(demultiplexer_2_out1), .out(divider_1_out), .rem(divider_1_rem));  // open: upper
  assign {out_7, out_10[30:0]} = decoder_1_out10 ? divider_1_rem : 32'bz;  // Controlled_Buffer controlled_buffer_4
  Comparator #(.width(32)) comparator_1 (
    .a(pull_resistor_1_node), .b(demultiplexer_2_out1), .gt(comparator_1_gt));  // open: eq, lt
  Negator #(.width(32)) negator_1 (.in(demultiplexer_2_out1), .out(negator_1_out));
  assign xor_1_out = pull_resistor_1_node ^ demultiplexer_2_out1;  // XOR_Gate xor_1, 32 bits wide
  assign or_3_out = pull_resistor_1_node | demultiplexer_2_out1;  // OR_Gate or_3, 32 bits wide
  assign and_1_out = pull_resistor_1_node & demultiplexer_2_out1;  // AND_Gate and_1, 32 bits wide
  assign not_3_out = ~pull_resistor_1_node;  // NOT_Gate not_3, 32 bits wide
  and and_2 (and_2_out, decoder_1_out4, demultiplexer_2_out1[31]);
  and and_3 (and_3_out, demultiplexer_2_out1[0], decoder_1_out5);
  assign {out_7, out_10[30:0]} = decoder_1_out12 ? subtractor_2_out : 32'bz;  // Controlled_Buffer controlled_buffer_5
  or or_4 (or_4_out, subtractor_1_bout, subtractor_2_bout);
  or or_5 (or_5_out, decoder_1_out0, decoder_1_out11);
  FPU fpu_1 (
    .in_1(demultiplexer_1_out0), .in_2(demultiplexer_2_out0), .in_3(in_4), .out_5({out_7, out_10[30:0]}),
    .out_4(out_5), .out_6(fpu_1_out_6));  // open: out_7
  assign {out_7, out_10[30:0]} = decoder_1_out14 ? demultiplexer_2_out1 : 32'bz;  // Controlled_Buffer controlled_buffer_6
  assign {out_7, out_10[30:0]} = decoder_1_out13 ? negator_1_out : 32'bz;  // Controlled_Buffer controlled_buffer_7
  assign {out_7, out_10[30:0]} = decoder_1_out9 ? xor_1_out : 32'bz;  // Controlled_Buffer controlled_buffer_8
  assign {out_7, out_10[30:0]} = decoder_1_out8 ? or_3_out : 32'bz;  // Controlled_Buffer controlled_buffer_9
  assign {out_7, out_10[30:0]} = decoder_1_out7 ? and_1_out : 32'bz;  // Controlled_Buffer controlled_buffer_10
  assign {out_7, out_10[30:0]} = decoder_1_out6 ? not_3_out : 32'bz;  // Controlled_Buffer controlled_buffer_11
  assign {out_7, out_10[30:0]} = decoder_1_out4 ? {demultiplexer_2_out1[30:0], or_2_out[0]} : 32'bz;  // Controlled_Buffer controlled_buffer_12
  or or_6 (or_6_out, and_2_out, and_3_out);
  assign {out_7, out_10[30:0]} = decoder_1_out5 ? {or_2_out[0], demultiplexer_2_out1[31:1]} : 32'bz;  // Controlled_Buffer controlled_buffer_13
  assign {out_7, out_10[30:0]} = or_5_out ? adder_1_out : 32'bz;  // Controlled_Buffer controlled_buffer_14
  and and_4 (and_4_out, adder_1_cout, or_5_out);
  assign {out_7, out_10[30:0]} = or_7_out ? subtractor_1_out : 32'bz;  // Controlled_Buffer controlled_buffer_15
  or or_7 (or_7_out, decoder_1_out15, decoder_1_out1);
  and and_5 (and_5_out, or_4_out, decoder_1_out1);
  assign {out_7, out_10[30:0]} = decoder_1_out2 ? multiplier_1_out : 32'bz;  // Controlled_Buffer controlled_buffer_16
  assign {out_7, out_10[30:0]} = decoder_1_out3 ? divider_1_out : 32'bz;  // Controlled_Buffer controlled_buffer_17
  Decoder #(.select(4)) decoder_1 (
    .out0(decoder_1_out0), .out1(decoder_1_out1), .out2(decoder_1_out2), .out3(decoder_1_out3),
    .out4(decoder_1_out4), .out5(decoder_1_out5), .out6(decoder_1_out6), .out7(decoder_1_out7),
    .out8(decoder_1_out8), .out9(decoder_1_out9), .out10(decoder_1_out10), .out11(decoder_1_out11),
    .out12(decoder_1_out12), .out13(decoder_1_out13), .out14(decoder_1_out14), .out15(decoder_1_out15),
    .sel(in_4[3:0]), .en(not_4_out));
  not not_4 (not_4_out, in_4[4]);
  or or_8 (out_9, or_6_out, and_4_out, and_5_out);
  Multiplexer multiplexer_1 (.in0(fpu_1_out_6), .in1(comparator_1_gt), .out(out_6), .sel(not_2_out));
  Pull_Resistor pull_resistor_4 (.node({out_7, out_10[30:0]}));
  BitFinder #(.width(32)) bitfinder_1 (.in({out_7, out_10[30:0]}), .found(bitfinder_1_found));  // open: index
  not not_5 (out_8, bitfinder_1_found);
  Pull_Resistor pull_resistor_5 (.node(out_9));

  assign out_10[31] = out_7;
endmodule

module INTRUCTION_REGISTER (
  input  [31:0] in_1,
  input  in_2,
  output [15:0] out_3
);

  Register #(.width(16)) register_1 (.D(in_1[15:0]), .Q(out_3), .clk(in_2));  // open: en, clr
endmodule

module REGISTER (
  input  [31:0] in_1,
  input  in_2,
  input  in_3,
  output [31:0] out_4
);

  wire [31:0] register_1_q;

  assign out_4 = in_3 ? register_1_q : 32'bz;  // Controlled_Buffer controlled_buffer_1
  Register #(.width(32)) register_1 (.D(in_1), .Q(register_1_q), .clk(in_2));  // open: en, clr
endmodule

module CLOCK (
  input  in_1,
  output out_2,
  output out_3,
  output out_4
);

  wire buffer_1_out_2, buffer_2_out_2;

  buffer buffer_1 (.in_1(in_1), .out_2(buffer_1_out_2));
  buffer buffer_2 (.in_1(buffer_1_out_2), .out_2(buffer_2_out_2));
  and and_1 (out_2, buffer_2_out_2, in_1);
  or or_1 (out_4, buffer_2_out_2, in_1);

  assign out_3 = in_1;
endmodule

module FLAG_REG (
  input  in_1,
  input  in_2,
  input  in_3,
  input  in_4,
  input  in_5,
  output out_6,
  output out_7,
  output out_8,
  output out_9
);

  Register #(.trigger("high"), .width(1)) register_1 (.D(in_1), .Q(out_6), .clk(in_5));  // open: en, clr
  Register #(.trigger("high"), .width(1)) register_2 (.D(in_2), .Q(out_7), .clk(in_5));  // open: en, clr
  Register #(.trigger("high"), .width(1)) register_3 (.D(in_3), .Q(out_8), .clk(in_5));  // open: en, clr
  Register #(.trigger("high"), .width(1)) register_4 (.D(in_4), .Q(out_9), .clk(in_5));  // open: en, clr
endmodule

module TMP (
  input  [31:0] in_1,
  input  in_2,
  input  in_3,
  output [31:0] out_4
);

  wire not_1_out;
  wire [0:0] controlled_buffer_1_out;
  wire [31:0] register_1_q;

  Register #(.width(32)) register_1 (.D(in_1), .Q(register_1_q), .clk(in_2));  // open: en, clr
  assign {out_4[31:1], controlled_buffer_1_out[0]} = not_1_out ? register_1_q : 32'bz;  // Controlled_Buffer controlled_buffer_1
  Pull_Resistor pull_resistor_1 (.node({out_4[31:1], controlled_buffer_1_out[0]}));
  not not_1 (not_1_out, in_3);
  or or_1 (out_4[0], controlled_buffer_1_out[0], in_3);
endmodule

module ACC (
  input  [31:0] in_1,
  input  in_2,
  input  in_3,
  output [31:0] out_4
);

  wire [31:0] register_1_q;

  Register #(.trigger("high"), .width(32)) register_1 (.D(in_1), .Q(register_1_q), .clk(in_2));  // open: en, clr
  assign out_4 = in_3 ? register_1_q : 32'bz;  // Controlled_Buffer controlled_buffer_1
endmodule

module IAR (
  input  enable,
  input  clock,
  input  reset,
  input  set,
  input  [31:0] in_5,
  output [31:0] out_6
);

  wire and_1_out, and_2_out, and_3_out, and_4_out, and_5_out, and_6_out, and_7_out, and_8_out, and_9_out,
       and_10_out, and_11_out, and_12_out, and_13_out, and_14_out, and_15_out, and_16_out, and_17_out,
       and_18_out, and_19_out, and_20_out, and_21_out, and_22_out, and_23_out, and_24_out, and_25_out,
       and_26_out, and_27_out, and_28_out, and_29_out, and_30_out, and_31_out, and_32_out, and_33_out,
       and_34_out, or_1_out, or_2_out, or_3_out, or_4_out, or_5_out, or_6_out, or_7_out, or_8_out, or_9_out,
       or_10_out, or_11_out, or_12_out, or_13_out, or_14_out, or_15_out, or_16_out, or_17_out, t_ff_1_qn,
       t_ff_2_qn, t_ff_3_qn, t_ff_4_qn, t_ff_5_qn, t_ff_6_qn, t_ff_7_qn, t_ff_8_qn, t_ff_9_qn, t_ff_10_qn,
       t_ff_11_qn, t_ff_12_qn, t_ff_13_qn, t_ff_14_qn, t_ff_15_qn, t_ff_16_qn;
  wire [16:0] t_ff_1_q;

  and and_1 (and_1_out, in_5[0], set);
  T_Flip_Flop t_ff_1 (.clk(clock), .T(1'b1), .Q(t_ff_1_q[0]), .Qn(t_ff_1_qn), .preset(and_1_out), .reset(or_1_out));
  or or_1 (or_1_out, reset, and_2_out);
  and and_2 (and_2_out, ~in_5[0], set);  // AND_Gate
  and and_3 (and_3_out, in_5[1], set);
  T_Flip_Flop t_ff_2 (.clk(t_ff_1_qn), .T(1'b1), .Q(t_ff_1_q[1]), .Qn(t_ff_2_qn), .preset(and_3_out), .reset(or_2_out));
  or or_2 (or_2_out, reset, and_4_out);
  and and_4 (and_4_out, ~in_5[1], set);  // AND_Gate
  and and_5 (and_5_out, in_5[2], set);
  T_Flip_Flop t_ff_3 (.clk(t_ff_2_qn), .T(1'b1), .Q(t_ff_1_q[2]), .Qn(t_ff_3_qn), .preset(and_5_out), .reset(or_3_out));
  or or_3 (or_3_out, reset, and_6_out);
  and and_6 (and_6_out, ~in_5[2], set);  // AND_Gate
  and and_7 (and_7_out, in_5[3], set);
  T_Flip_Flop t_ff_4 (.clk(t_ff_3_qn), .T(1'b1), .Q(t_ff_1_q[3]), .Qn(t_ff_4_qn), .preset(and_7_out), .reset(or_4_out));
  or or_4 (or_4_out, reset, and_8_out);
  and and_8 (and_8_out, ~in_5[3], set);  // AND_Gate
  and and_9 (and_9_out, in_5[4], set);
  T_Flip_Flop t_ff_5 (.clk(t_ff_4_qn), .T(1'b1), .Q(t_ff_1_q[4]), .Qn(t_ff_5_qn), .preset(and_9_out), .reset(or_5_out));
  or or_5 (or_5_out, reset, and_10_out);
  and and_10 (and_10_out, ~in_5[4], set);  // AND_Gate
  and and_11 (and_11_out, in_5[5], set);
  T_Flip_Flop t_ff_6 (
    .clk(t_ff_5_qn), .T(1'b1), .Q(t_ff_1_q[5]), .Qn(t_ff_6_qn), .preset(and_11_out), .reset(or_6_out));
  or or_6 (or_6_out, reset, and_12_out);
  and and_12 (and_12_out, ~in_5[5], set);  // AND_Gate
  and and_13 (and_13_out, in_5[6], set);
  T_Flip_Flop t_ff_7 (
    .clk(t_ff_6_qn), .T(1'b1), .Q(t_ff_1_q[6]), .Qn(t_ff_7_qn), .preset(and_13_out), .reset(or_7_out));
  or or_7 (or_7_out, reset, and_14_out);
  and and_14 (and_14_out, ~in_5[6], set);  // AND_Gate
  and and_15 (and_15_out, in_5[7], set);
  T_Flip_Flop t_ff_8 (
    .clk(t_ff_7_qn), .T(1'b1), .Q(t_ff_1_q[7]), .Qn(t_ff_8_qn), .preset(and_15_out), .reset(or_8_out));
  or or_8 (or_8_out, reset, and_16_out);
  and and_16 (and_16_out, ~in_5[7], set);  // AND_Gate
  and and_17 (and_17_out, in_5[8], set);
  T_Flip_Flop t_ff_9 (
    .clk(t_ff_8_qn), .T(1'b1), .Q(t_ff_1_q[8]), .Qn(t_ff_9_qn), .preset(and_17_out), .reset(or_9_out));
  or or_9 (or_9_out, reset, and_19_out);
  and and_18 (and_18_out, in_5[9], set);
  and and_19 (and_19_out, ~in_5[8], set);  // AND_Gate
  T_Flip_Flop t_ff_10 (
    .clk(t_ff_9_qn), .T(1'b1), .Q(t_ff_1_q[9]), .Qn(t_ff_10_qn), .preset(and_18_out), .reset(or_10_out));
  or or_10 (or_10_out, reset, and_20_out);
  and and_20 (and_20_out, ~in_5[9], set);  // AND_Gate
  and and_21 (and_21_out, in_5[10], set);
  assign out_6 = enable ? {{15{1'b0}}, t_ff_1_q} : 32'bz;  // Controlled_Buffer controlled_buffer_1
  T_Flip_Flop t_ff_11 (
    .clk(t_ff_10_qn), .T(1'b1), .Q(t_ff_1_q[10]), .Qn(t_ff_11_qn), .preset(and_21_out), .reset(or_11_out));
  or or_11 (or_11_out, reset, and_22_out);
  and and_22 (and_22_out, ~in_5[10], set);  // AND_Gate
  and and_23 (and_23_out, in_5[11], set);
  T_Flip_Flop t_ff_12 (
    .clk(t_ff_11_qn), .T(1'b1), .Q(t_ff_1_q[11]), .Qn(t_ff_12_qn), .preset(and_23_out), .reset(or_12_out));
  or or_12 (or_12_out, reset, and_24_out);
  and and_24 (and_24_out, ~in_5[11], set);  // AND_Gate
  and and_25 (and_25_out, in_5[12], set);
  T_Flip_Flop t_ff_13 (
    .clk(t_ff_12_qn), .T(1'b1), .Q(t_ff_1_q[12]), .Qn(t_ff_13_qn), .preset(and_25_out), .reset(or_13_out));
  or or_13 (or_13_out, reset, and_26_out);
  and and_26 (and_26_out, ~in_5[12], set);  // AND_Gate
  and and_27 (and_27_out, in_5[13], set);
  T_Flip_Flop t_ff_14 (
    .clk(t_ff_13_qn), .T(1'b1), .Q(t_ff_1_q[13]), .Qn(t_ff_14_qn), .preset(and_27_out), .reset(or_14_out));
  or or_14 (or_14_out, reset, and_28_out);
  and and_28 (and_28_out, ~in_5[13], set);  // AND_Gate
  and and_29 (and_29_out, in_5[14], set);
  T_Flip_Flop t_ff_15 (
    .clk(t_ff_14_qn), .T(1'b1), .Q(t_ff_1_q[14]), .Qn(t_ff_15_qn), .preset(and_29_out), .reset(or_15_out));
  or or_15 (or_15_out, reset, and_30_out);
  and and_30 (and_30_out, ~in_5[14], set);  // AND_Gate
  and and_31 (and_31_out, in_5[15], set);
  T_Flip_Flop t_ff_16 (
    .clk(t_ff_15_qn), .T(1'b1), .Q(t_ff_1_q[15]), .Qn(t_ff_16_qn), .preset(and_31_out), .reset(or_16_out));
  or or_16 (or_16_out, reset, and_32_out);
  and and_32 (and_32_out, ~in_5[15], set);  // AND_Gate
  and and_33 (and_33_out, in_5[16], set);
  T_Flip_Flop t_ff_17 (
    .clk(t_ff_16_qn), .T(1'b1), .Q(t_ff_1_q[16]), .preset(and_33_out), .reset(or_17_out));  // open: Qn
  or or_17 (or_17_out, reset, and_34_out);
  and and_34 (and_34_out, ~in_5[16], set);  // AND_Gate
endmodule

module KEYBOARD (
  input  [6:0] in_1,
  input  [31:0] in_2,
  input  [3:0] in_3,
  output [31:0] out_4,
  output out_5
);

  wire and_1_out, and_2_out, and_3_out, and_4_out, and_5_out, and_6_out, d_ff_1_q, not_1_out, not_2_out,
       not_3_out, or_1_out, or_2_out;

  assign out_4 = and_6_out ? {{25{1'b0}}, in_1} : 32'bz;  // Controlled_Buffer controlled_buffer_1
  or or_1 (or_1_out, in_2[0], in_2[1], in_2[2]);
  and and_1 (and_1_out, in_2[4], in_2[5], in_2[6]);
  or or_2 (or_2_out, or_1_out, in_2[3]);
  not not_1 (not_1_out, or_2_out);
  and and_2 (and_2_out, not_1_out, and_3_out);
  and and_3 (and_3_out, and_1_out, in_2[7]);
  Register #(.width(1)) register_1 (.D(1'b1), .clk(d_ff_1_q));  // open: en, Q, clr
  not not_2 (not_2_out, in_3[3]);
  not not_3 (not_3_out, in_3[2]);
  D_Flip_Flop d_ff_1 (.clk(and_4_out), .D(and_2_out), .Q(d_ff_1_q));  // open: Qn, preset, reset
  and and_4 (and_4_out, in_3[0], in_3[2], in_3[3]);
  and and_5 (and_5_out, in_3[1], not_2_out, not_3_out);
  and and_6 (and_6_out, d_ff_1_q, and_5_out);
  not not_4 (out_5, and_6_out);
  T_Flip_Flop t_ff_1 (.clk(and_2_out), .T(1'b1));  // open: Q, Qn, preset, reset

  // Notes on the sheet:
  //   CLOCK S
  //   CLK E
  //   D/A
  //   I/O
endmodule

module NUMBER_DISPLAY (
  input  [31:0] in_1,
  input  [3:0] in_2,
  output [3:0] out_3,
  output [3:0] out_4,
  output [3:0] out_5,
  output [3:0] out_6,
  output [3:0] out_7,
  output [3:0] out_8,
  output [3:0] out_9,
  output [3:0] out_10
);

  wire and_1_out, and_2_out, and_3_out, and_4_out, d_ff_1_q, not_1_out, not_2_out, not_3_out, not_4_out,
       not_5_out;

  not not_1 (not_1_out, in_1[0]);
  not not_2 (not_2_out, in_1[1]);
  not not_3 (not_3_out, in_1[6]);
  not not_4 (not_4_out, in_1[7]);
  Register #(.width(32)) register_1 (
    .D(in_1), .Q({out_10, out_9, out_8, out_7, out_6, out_5, out_4, out_3}), .clk(and_4_out));  // open: en, clr
  and and_1 (and_1_out, 1'b1, not_1_out, not_2_out, in_1[2], in_1[3], in_1[4], in_1[5], not_3_out, not_4_out);
  not not_5 (not_5_out, in_2[2]);
  D_Flip_Flop d_ff_1 (.clk(and_2_out), .D(and_1_out), .Q(d_ff_1_q));  // open: Qn, preset, reset
  and and_2 (and_2_out, in_2[0], in_2[2], in_2[3]);
  and and_3 (and_3_out, in_2[1], in_2[3], not_5_out);
  and and_4 (and_4_out, d_ff_1_q, and_3_out);

  // Notes on the sheet:
  //   CLOCK S
  //   CLK E
  //   D/A
  //   I/O
endmodule

module program_loader (
  input  in_1
);

  ROM_part rom_1 ();  // open: addr, data
endmodule

module teste (
  input  [31:0] in_1,
  input  [31:0] in_2,
  input  [31:0] in_3,
  input  in_4,
  input  [31:0] in_5,
  input  in_6,
  input  _1_SUB
);

  wire bitfinder_1_found, bitfinder_2_found, bitfinder_3_found, bitfinder_7_found, comparator_1_lt,
       not_4_out, not_6_out, not_7_out, not_8_out, or_1_out, or_2_out, pull_resistor_6_node,
       pull_resistor_7_node, pull_resistor_8_node, pull_resistor_9_node, subtractor_1_bout,
       subtractor_3_bout, subtractor_4_bout, subtractor_5_bout, subtractor_6_bout, xor_1_out;
  wire [2:0] pull_resistor_10_node, pull_resistor_11_node;
  wire [4:0] bit_extender_7_out, bit_extender_12_out, bitfinder_1_index, bitfinder_2_index,
       bitfinder_3_index, bitfinder_7_index, multiplexer_1_out, multiplexer_2_out, multiplexer_3_out,
       multiplexer_5_out, multiplexer_17_out, not_1_out, not_2_out, not_3_out, not_5_out, subtractor_1_out,
       subtractor_3_out, subtractor_4_out, subtractor_5_out, subtractor_8_out;
  wire [7:0] adder_1_out, adder_2_out, adder_3_out, adder_6_out, bit_extender_4_out, bit_extender_5_out,
       bit_extender_6_out, bit_extender_13_out, multiplexer_14_out, multiplexer_15_out, multiplexer_18_out,
       multiplexer_19_out, multiplexer_20_out, multiplexer_21_out, multiplexer_23_out, negator_1_out,
       negator_2_out, pull_resistor_2_node, pull_resistor_4_node, pull_resistor_5_node_2, subtractor_2_out,
       subtractor_6_out, subtractor_9_out;
  wire [22:0] adder_7_out, bit_extender_8_out, bit_extender_9_out, bit_extender_10_out, bit_extender_16_out,
       multiplexer_22_out, pull_resistor_2_node_3, pull_resistor_4_node_3, pull_resistor_5_node;
  wire [23:0] multiplier_1_cout, shifter_11_out;
  wire [23:23] bitfinder_4_found;
  wire [26:0] adder_4_out, multiplexer_9_out, multiplexer_10_out, multiplexer_12_out, multiplexer_13_out,
       multiplexer_16_out, shifter_9_out, subtractor_7_out;
  wire [26:26] bitfinder_5_found, bitfinder_6_found;
  wire [27:0] shifter_10_out;
  wire [27:27] adder_4_cout;
  wire [30:0] bit_extender_11_out, controlled_buffer_2_out, multiplexer_11_out, shifter_7_out, shifter_8_out;
  wire [31:0] bit_extender_1_out, bit_extender_2_out, bit_extender_3_out, controlled_buffer_1_out,
       multiplexer_4_out, multiplexer_6_out, multiplexer_7_out, shifter_1_out, shifter_2_out, shifter_3_out,
       shifter_4_out, shifter_5_out, shifter_6_out;
  wire [31:23] adder_5_out;
  wire [31:31] controlled_buffer_2_out_2, pull_resistor_2_node_2, pull_resistor_4_node_2,
       pull_resistor_5_node_3, xor_2_out;
  wire [63:0] bit_extender_14_out, bit_extender_15_out, divider_1_out;

  assign controlled_buffer_1_out = in_4 ? 32'h6252 : 32'bz;  // Controlled_Buffer controlled_buffer_1
  Pull_Resistor pull_resistor_1 (.node(controlled_buffer_1_out));
  Pull_Resistor pull_resistor_2 (.node({pull_resistor_2_node_2[31], pull_resistor_2_node, pull_resistor_2_node_3}));
  assign {controlled_buffer_2_out_2[31], controlled_buffer_2_out} = in_4 ? 32'h2ac : 32'bz;  // Controlled_Buffer controlled_buffer_2
  Pull_Resistor pull_resistor_3 (.node({controlled_buffer_2_out_2[31], controlled_buffer_2_out}));
  Pull_Resistor pull_resistor_4 (.node({pull_resistor_4_node_2[31], pull_resistor_4_node, pull_resistor_4_node_3}));
  BitFinder #(.\type ("high1"), .width(32)) bitfinder_1 (
    .in(bit_extender_1_out), .index(bitfinder_1_index), .found(bitfinder_1_found));
  assign bit_extender_1_out = {{1{1'b0}}, in_2[30:0]};  // Bit_Extender bit_extender_1
  Pull_Resistor pull_resistor_5 (.node({pull_resistor_5_node_3[31], pull_resistor_5_node_2, pull_resistor_5_node}));
  BitFinder #(.\type ("high1"), .width(32)) bitfinder_2 (
    .in(bit_extender_2_out), .index(bitfinder_2_index), .found(bitfinder_2_found));
  assign bit_extender_2_out = {{1{1'b0}}, controlled_buffer_1_out[30:0]};  // Bit_Extender bit_extender_2
  BitFinder #(.\type ("high1"), .width(32)) bitfinder_3 (
    .in(bit_extender_3_out), .index(bitfinder_3_index), .found(bitfinder_3_found));
  assign bit_extender_3_out = {{1{1'b0}}, controlled_buffer_2_out};  // Bit_Extender bit_extender_3
  Pull_Resistor pull_resistor_6 (.node(pull_resistor_6_node));
  Subtractor #(.width(5)) subtractor_1 (
    .a(5'b10111), .b(bitfinder_1_index), .out(subtractor_1_out), .bin(pull_resistor_6_node),
    .bout(subtractor_1_bout));
  assign pull_resistor_6_node = bitfinder_1_found ? subtractor_1_bout : 1'bz;  // Controlled_Buffer controlled_buffer_3
  assign bit_extender_4_out = {{3{1'b0}}, bitfinder_1_index};  // Bit_Extender bit_extender_4
  Subtractor subtractor_2 (.a(pull_resistor_5_node_2), .b(8'h7f), .out(subtractor_2_out));  // open: bin, bout
  Pull_Resistor pull_resistor_7 (.node(pull_resistor_7_node));
  Subtractor #(.width(5)) subtractor_3 (
    .a(5'b10111), .b(bitfinder_2_index), .out(subtractor_3_out), .bin(pull_resistor_7_node),
    .bout(subtractor_3_bout));
  assign pull_resistor_7_node = bitfinder_2_found ? subtractor_3_bout : 1'bz;  // Controlled_Buffer controlled_buffer_4
  assign bit_extender_5_out = {{3{1'b0}}, bitfinder_2_index};  // Bit_Extender bit_extender_5
  Pull_Resistor pull_resistor_8 (.node(pull_resistor_8_node));
  Subtractor #(.width(5)) subtractor_4 (
    .a(5'b10111), .b(bitfinder_3_index), .out(subtractor_4_out), .bin(pull_resistor_8_node),
    .bout(subtractor_4_bout));
  assign pull_resistor_8_node = bitfinder_3_found ? subtractor_4_bout : 1'bz;  // Controlled_Buffer controlled_buffer_5
  assign bit_extender_6_out = {{3{1'b0}}, bitfinder_3_index};  // Bit_Extender bit_extender_6
  Multiplexer #(.width(5)) multiplexer_1 (
    .in0(subtractor_1_out), .in1(not_1_out), .out(multiplexer_1_out), .sel(pull_resistor_6_node));
  assign not_1_out = ~subtractor_1_out;  // NOT_Gate not_1, 5 bits wide
  Adder adder_1 (.a(8'h7f), .b(bit_extender_4_out), .out(adder_1_out));  // open: cin, cout
  Pull_Resistor pull_resistor_9 (.node(pull_resistor_9_node));
  Bit_Extender #(.out_width(5), .\type ("zero")) bit_extender_7 (.in(subtractor_2_out), .out(bit_extender_7_out));
  Multiplexer #(.width(5)) multiplexer_2 (
    .in0(subtractor_3_out), .in1(not_2_out), .out(multiplexer_2_out), .sel(pull_resistor_7_node));
  assign not_2_out = ~subtractor_3_out;  // NOT_Gate not_2, 5 bits wide
  Adder adder_2 (.a(8'h7f), .b(bit_extender_5_out), .out(adder_2_out));  // open: cin, cout
  Multiplexer #(.width(5)) multiplexer_3 (
    .in0(subtractor_4_out), .in1(not_3_out), .out(multiplexer_3_out), .sel(pull_resistor_8_node));
  assign not_3_out = ~subtractor_4_out;  // NOT_Gate not_3, 5 bits wide
  Adder adder_3 (.a(8'h7f), .b(bit_extender_6_out), .out(adder_3_out));  // open: cin, cout
  Shifter #(.shift("lr"), .width(32)) shifter_1 (
    .in(bit_extender_1_out), .\dist (multiplexer_1_out), .out(shifter_1_out));
  Shifter #(.width(32)) shifter_2 (.in(bit_extender_1_out), .\dist (multiplexer_1_out), .out(shifter_2_out));
  not not_4 (not_4_out, pull_resistor_6_node);
  Subtractor #(.width(5)) subtractor_5 (
    .a(5'b10111), .b(bit_extender_7_out), .out(subtractor_5_out), .bin(pull_resistor_9_node),
    .bout(subtractor_5_bout));
  assign not_5_out = ~subtractor_5_out;  // NOT_Gate not_5, 5 bits wide
  assign pull_resistor_9_node = bitfinder_4_found[23] ? subtractor_5_bout : 1'bz;  // Controlled_Buffer controlled_buffer_6
  BitFinder #(.\type ("high1"), .width(32)) bitfinder_4 (
    .in({pull_resistor_5_node_3[31], pull_resistor_5_node_2, pull_resistor_5_node}),
    .found(bitfinder_4_found[23]));  // open: index
  Shifter #(.shift("lr"), .width(32)) shifter_3 (
    .in(bit_extender_2_out), .\dist (multiplexer_2_out), .out(shifter_3_out));
  Shifter #(.width(32)) shifter_4 (.in(bit_extender_2_out), .\dist (multiplexer_2_out), .out(shifter_4_out));
  not not_6 (not_6_out, pull_resistor_7_node);
  Shifter #(.shift("lr"), .width(32)) shifter_5 (
    .in(bit_extender_3_out), .\dist (multiplexer_3_out), .out(shifter_5_out));
  Shifter #(.width(32)) shifter_6 (.in(bit_extender_3_out), .\dist (multiplexer_3_out), .out(shifter_6_out));
  not not_7 (not_7_out, pull_resistor_8_node);
  ExactlyOne xor_1 (.out(xor_1_out), .in0(_1_SUB), .in1(pull_resistor_2_node_2[31]), .in2(pull_resistor_4_node_2[31]));
  Bit_Extender #(.in_width(32), .out_width(23), .\type ("zero")) bit_extender_8 (
    .in(multiplexer_4_out), .out(bit_extender_8_out));
  Multiplexer #(.width(32)) multiplexer_4 (
    .in0(shifter_1_out), .in1(shifter_2_out), .out(multiplexer_4_out), .sel(not_4_out));
  Multiplexer #(.width(5)) multiplexer_5 (
    .in0(subtractor_5_out), .in1(not_5_out), .out(multiplexer_5_out), .sel(pull_resistor_9_node));
  Bit_Extender #(.in_width(32), .out_width(23), .\type ("zero")) bit_extender_9 (
    .in(multiplexer_6_out), .out(bit_extender_9_out));
  Multiplexer #(.width(32)) multiplexer_6 (
    .in0(shifter_3_out), .in1(shifter_4_out), .out(multiplexer_6_out), .sel(not_6_out));
  Bit_Extender #(.in_width(32), .out_width(23), .\type ("zero")) bit_extender_10 (
    .in(multiplexer_7_out), .out(bit_extender_10_out));
  Multiplexer #(.width(32)) multiplexer_7 (
    .in0(shifter_5_out), .in1(shifter_6_out), .out(multiplexer_7_out), .sel(not_7_out));
  Pull_Resistor pull_resistor_10 (.node(pull_resistor_10_node));
  BitFinder #(.\type ("high1")) bitfinder_5 (.in(pull_resistor_2_node), .found(bitfinder_5_found[26]));  // open: index
  Multiplexer multiplexer_8 (
    .in0(pull_resistor_2_node_2[31]), .in1(pull_resistor_4_node_2[31]), .out(adder_5_out[31]),
    .sel(comparator_1_lt));
  Pull_Resistor pull_resistor_11 (.node(pull_resistor_11_node));
  BitFinder #(.\type ("high1")) bitfinder_6 (.in(pull_resistor_4_node), .found(bitfinder_6_found[26]));  // open: index
  assign {pull_resistor_5_node_3[31], pull_resistor_5_node_2, pull_resistor_5_node} = bitfinder_1_found ? {in_2[31], adder_1_out, bit_extender_8_out} : 32'bz;  // Controlled_Buffer controlled_buffer_7
  assign bit_extender_11_out = {{7{1'b0}}, {bitfinder_4_found[23], pull_resistor_5_node}};  // Bit_Extender bit_extender_11
  assign {pull_resistor_2_node_2[31], pull_resistor_2_node, pull_resistor_2_node_3} = bitfinder_2_found ? {controlled_buffer_1_out[31], adder_2_out, bit_extender_9_out} : 32'bz;  // Controlled_Buffer controlled_buffer_8
  assign {pull_resistor_4_node_2[31], pull_resistor_4_node, pull_resistor_4_node_3} = bitfinder_3_found ? {controlled_buffer_2_out_2[31], adder_3_out, bit_extender_10_out} : 32'bz;  // Controlled_Buffer controlled_buffer_9
  Multiplexer #(.width(27)) multiplexer_9 (
    .in0({bitfinder_6_found[26], pull_resistor_4_node_3, pull_resistor_11_node}),
    .in1({bitfinder_5_found[26], pull_resistor_2_node_3, pull_resistor_10_node}), .out(multiplexer_9_out),
    .sel(comparator_1_lt));
  Multiplexer #(.width(27)) multiplexer_10 (
    .in0({bitfinder_5_found[26], pull_resistor_2_node_3, pull_resistor_10_node}),
    .in1({bitfinder_6_found[26], pull_resistor_4_node_3, pull_resistor_11_node}), .out(multiplexer_10_out),
    .sel(comparator_1_lt));
  Comparator comparator_1 (.a(pull_resistor_2_node), .b(pull_resistor_4_node), .lt(comparator_1_lt));  // open: gt, eq
  Subtractor subtractor_6 (
    .a(pull_resistor_2_node), .b(pull_resistor_4_node), .out(subtractor_6_out), .bout(subtractor_6_bout));  // open: bin
  // Probe on {pull_resistor_5_node_3[31], pull_resistor_5_node_2, pull_resistor_5_node}
  Shifter #(.shift("lr"), .width(31)) shifter_7 (
    .in(bit_extender_11_out), .\dist (multiplexer_5_out), .out(shifter_7_out));
  Multiplexer #(.width(31)) multiplexer_11 (
    .in0(shifter_7_out), .in1(shifter_8_out), .out(multiplexer_11_out), .sel(pull_resistor_9_node));
  Shifter #(.width(31)) shifter_8 (.in(bit_extender_11_out), .\dist (multiplexer_5_out), .out(shifter_8_out));
  Shifter #(.shift("lr"), .width(27)) shifter_9 (
    .in(multiplexer_9_out), .\dist (bit_extender_12_out), .out(shifter_9_out));
  Negator negator_1 (.in(subtractor_6_out), .out(negator_1_out));
  RAM_part #(.addrWidth(2), .dataWidth(32)) ram_1 ();  // open: addr, we, oe, clk, din, dout
  // Probe on {pull_resistor_5_node_3[31], multiplexer_11_out}
  Multiplexer #(.width(27)) multiplexer_12 (
    .in0(multiplexer_10_out), .in1(shifter_9_out), .out(multiplexer_12_out), .sel(comparator_1_lt));
  Multiplexer #(.width(27)) multiplexer_13 (
    .in0(shifter_9_out), .in1(multiplexer_10_out), .out(multiplexer_13_out), .sel(comparator_1_lt));
  Multiplexer #(.width(8)) multiplexer_14 (
    .in0(pull_resistor_2_node), .in1(pull_resistor_4_node), .out(multiplexer_14_out), .sel(comparator_1_lt));
  Bit_Extender #(.out_width(5), .\type ("zero")) bit_extender_12 (.in(multiplexer_15_out), .out(bit_extender_12_out));
  Multiplexer #(.width(8)) multiplexer_15 (
    .in0(subtractor_6_out), .in1(negator_1_out), .out(multiplexer_15_out), .sel(subtractor_6_bout));
  Adder #(.width(27)) adder_4 (
    .a(multiplexer_12_out), .b(multiplexer_13_out), .out(adder_4_out), .cout(adder_4_cout[27]));  // open: cin
  Subtractor #(.width(27)) subtractor_7 (
    .a(multiplexer_12_out), .b(multiplexer_13_out), .out(subtractor_7_out));  // open: bin, bout
  Multiplexer #(.width(27)) multiplexer_16 (
    .in0(adder_4_out), .in1(subtractor_7_out), .out(multiplexer_16_out), .sel(xor_1_out));
  assign bit_extender_13_out = {{3{1'b0}}, subtractor_8_out};  // Bit_Extender bit_extender_13
  Negator negator_2 (.in(bit_extender_13_out), .out(negator_2_out));
  BitFinder #(.\type ("high1"), .width(28)) bitfinder_7 (
    .in({adder_4_cout[27], multiplexer_16_out}), .index(bitfinder_7_index), .found(bitfinder_7_found));
  Shifter #(.width(28)) shifter_10 (
    .in({adder_4_cout[27], multiplexer_16_out}), .\dist (subtractor_8_out), .out(shifter_10_out));
  Adder adder_5 (
    .a(negator_2_out), .b(multiplexer_14_out), .out(adder_5_out[30:23]), .cin(bitfinder_7_found));  // open: cout
  xor xor_2 (xor_2_out[31], pull_resistor_2_node_2[31], pull_resistor_4_node_2[31]);
  Multiplexer #(.width(5)) multiplexer_17 (
    .in0(5'b00001), .in1({5{1'b0}}), .out(multiplexer_17_out), .sel(multiplier_1_cout[23]));
  Multiplexer #(.width(8)) multiplexer_18 (
    .in0(pull_resistor_2_node), .in1(subtractor_9_out), .out(multiplexer_18_out), .sel(in_6));
  Multiplexer #(.width(8)) multiplexer_19 (
    .in0(adder_6_out), .in1(pull_resistor_2_node), .out(multiplexer_19_out), .sel(in_6));
  Subtractor #(.width(5)) subtractor_8 (
    .a(5'b11011), .b(bitfinder_7_index), .out(subtractor_8_out));  // open: bin, bout
  assign bit_extender_14_out = {{40{1'b0}}, {1'b1, pull_resistor_2_node_3}};  // Bit_Extender bit_extender_14
  Multiplier #(.width(24)) multiplier_1 (
    .a({1'b1, pull_resistor_2_node_3}), .b({1'b1, pull_resistor_4_node_3}), .cout(multiplier_1_cout));  // open: out, cin
  Shifter #(.width(24)) shifter_11 (.in(multiplier_1_cout), .\dist (multiplexer_17_out), .out(shifter_11_out));
  or or_1 (or_1_out, multiplier_1_cout[23], in_6);
  Multiplexer #(.width(8)) multiplexer_20 (
    .in0(pull_resistor_4_node), .in1(8'h7f), .out(multiplexer_20_out), .sel(in_6));
  Multiplexer #(.width(8)) multiplexer_21 (
    .in0(8'h7f), .in1(pull_resistor_4_node), .out(multiplexer_21_out), .sel(in_6));
  assign bit_extender_15_out = {{40{1'b0}}, {1'b1, pull_resistor_4_node_3}};  // Bit_Extender bit_extender_15
  Bit_Extender #(.in_width(24), .out_width(23), .\type ("zero")) bit_extender_16 (
    .in(shifter_11_out), .out(bit_extender_16_out));
  not not_8 (not_8_out, in_6);
  Adder adder_6 (.a(multiplexer_20_out), .b(multiplexer_18_out), .out(adder_6_out), .cin(or_1_out));  // open: cout
  Subtractor subtractor_9 (
    .a(multiplexer_19_out), .b(multiplexer_21_out), .out(subtractor_9_out), .bin(in_6));  // open: bout
  Divider #(.width(64)) divider_1 (
    .a({64{1'b0}}), .b(bit_extender_15_out), .out(divider_1_out), .upper(bit_extender_14_out));  // open: rem
  Multiplexer #(.width(23)) multiplexer_22 (
    .in0(adder_7_out), .in1(bit_extender_16_out), .out(multiplexer_22_out), .sel(not_8_out));
  Multiplexer #(.width(8)) multiplexer_23 (
    .in0(adder_6_out), .in1(subtractor_9_out), .out(multiplexer_23_out), .sel(not_8_out));
  or or_2 (or_2_out, divider_1_out[39], divider_1_out[40]);
  Adder #(.width(23)) adder_7 (
    .a(divider_1_out[63:41]), .b({23{1'b0}}), .out(adder_7_out), .cin(or_2_out));  // open: cout

  // Notes on the sheet:
  //   0-ADD
  //   0-MULT
  //   1-DIV
endmodule

module buffer (
  input  in_1,
  output out_2
);

  wire buffer_1_out, buffer_2_out, buffer_3_out, buffer_4_out, buffer_6_out, buffer_7_out, buffer_8_out,
       buffer_9_out, buffer_10_out, buffer_11_out, buffer_12_out, buffer_13_out, buffer_14_out,
       buffer_15_out, buffer_16_out, buffer_17_out, buffer_18_out, buffer_19_out, buffer_20_out,
       buffer_21_out, buffer_22_out, buffer_23_out, buffer_24_out, buffer_25_out, buffer_26_out,
       buffer_27_out, buffer_28_out, buffer_29_out, buffer_30_out, buffer_31_out, buffer_32_out,
       buffer_33_out, buffer_34_out, buffer_35_out, buffer_36_out, buffer_37_out, buffer_38_out,
       buffer_39_out, buffer_40_out, buffer_41_out, buffer_42_out, buffer_43_out, buffer_44_out,
       buffer_45_out, buffer_46_out, buffer_47_out, buffer_48_out, buffer_49_out, buffer_50_out,
       buffer_51_out, buffer_52_out, buffer_53_out, buffer_54_out, buffer_55_out, buffer_56_out,
       buffer_57_out, buffer_58_out, buffer_59_out, buffer_60_out, buffer_61_out, buffer_62_out,
       buffer_63_out, buffer_64_out, buffer_65_out, buffer_66_out, buffer_67_out, buffer_68_out,
       buffer_69_out, buffer_70_out, buffer_71_out, buffer_72_out, buffer_73_out, buffer_74_out,
       buffer_75_out, buffer_76_out, buffer_77_out, buffer_78_out, buffer_79_out, buffer_80_out,
       buffer_81_out, buffer_82_out, buffer_83_out, buffer_84_out, buffer_85_out, buffer_86_out,
       buffer_87_out, buffer_88_out, buffer_89_out, buffer_90_out, buffer_91_out, buffer_92_out,
       buffer_93_out, buffer_94_out, buffer_95_out, buffer_96_out, buffer_97_out, buffer_98_out,
       buffer_99_out, buffer_100_out, buffer_101_out, buffer_102_out, buffer_103_out, buffer_104_out,
       buffer_105_out, buffer_106_out, buffer_107_out, buffer_108_out, buffer_109_out, buffer_110_out,
       buffer_111_out, buffer_112_out, buffer_113_out, buffer_114_out, buffer_115_out, buffer_116_out,
       buffer_117_out, buffer_118_out, buffer_119_out, buffer_120_out, buffer_121_out, buffer_122_out,
       buffer_123_out, buffer_124_out, buffer_125_out, buffer_126_out, buffer_127_out, buffer_128_out;

  buf buffer_1 (buffer_1_out, in_1);
  buf buffer_2 (buffer_2_out, buffer_3_out);
  buf buffer_3 (buffer_3_out, buffer_11_out);
  buf buffer_4 (buffer_4_out, buffer_2_out);
  buf buffer_5 (out_2, buffer_6_out);
  buf buffer_6 (buffer_6_out, buffer_19_out);
  buf buffer_7 (buffer_7_out, buffer_1_out);
  buf buffer_8 (buffer_8_out, buffer_7_out);
  buf buffer_9 (buffer_9_out, buffer_8_out);
  buf buffer_10 (buffer_10_out, buffer_9_out);
  buf buffer_11 (buffer_11_out, buffer_12_out);
  buf buffer_12 (buffer_12_out, buffer_13_out);
  buf buffer_13 (buffer_13_out, buffer_14_out);
  buf buffer_14 (buffer_14_out, buffer_27_out);
  buf buffer_15 (buffer_15_out, buffer_4_out);
  buf buffer_16 (buffer_16_out, buffer_15_out);
  buf buffer_17 (buffer_17_out, buffer_16_out);
  buf buffer_18 (buffer_18_out, buffer_17_out);
  buf buffer_19 (buffer_19_out, buffer_20_out);
  buf buffer_20 (buffer_20_out, buffer_21_out);
  buf buffer_21 (buffer_21_out, buffer_22_out);
  buf buffer_22 (buffer_22_out, buffer_35_out);
  buf buffer_23 (buffer_23_out, buffer_10_out);
  buf buffer_24 (buffer_24_out, buffer_23_out);
  buf buffer_25 (buffer_25_out, buffer_24_out);
  buf buffer_26 (buffer_26_out, buffer_25_out);
  buf buffer_27 (buffer_27_out, buffer_28_out);
  buf buffer_28 (buffer_28_out, buffer_29_out);
  buf buffer_29 (buffer_29_out, buffer_30_out);
  buf buffer_30 (buffer_30_out, buffer_43_out);
  buf buffer_31 (buffer_31_out, buffer_18_out);
  buf buffer_32 (buffer_32_out, buffer_31_out);
  buf buffer_33 (buffer_33_out, buffer_32_out);
  buf buffer_34 (buffer_34_out, buffer_33_out);
  buf buffer_35 (buffer_35_out, buffer_36_out);
  buf buffer_36 (buffer_36_out, buffer_37_out);
  buf buffer_37 (buffer_37_out, buffer_38_out);
  buf buffer_38 (buffer_38_out, buffer_51_out);
  buf buffer_39 (buffer_39_out, buffer_26_out);
  buf buffer_40 (buffer_40_out, buffer_39_out);
  buf buffer_41 (buffer_41_out, buffer_40_out);
  buf buffer_42 (buffer_42_out, buffer_41_out);
  buf buffer_43 (buffer_43_out, buffer_44_out);
  buf buffer_44 (buffer_44_out, buffer_45_out);
  buf buffer_45 (buffer_45_out, buffer_46_out);
  buf buffer_46 (buffer_46_out, buffer_59_out);
  buf buffer_47 (buffer_47_out, buffer_34_out);
  buf buffer_48 (buffer_48_out, buffer_47_out);
  buf buffer_49 (buffer_49_out, buffer_48_out);
  buf buffer_50 (buffer_50_out, buffer_49_out);
  buf buffer_51 (buffer_51_out, buffer_52_out);
  buf buffer_52 (buffer_52_out, buffer_53_out);
  buf buffer_53 (buffer_53_out, buffer_54_out);
  buf buffer_54 (buffer_54_out, buffer_67_out);
  buf buffer_55 (buffer_55_out, buffer_42_out);
  buf buffer_56 (buffer_56_out, buffer_55_out);
  buf buffer_57 (buffer_57_out, buffer_56_out);
  buf buffer_58 (buffer_58_out, buffer_57_out);
  buf buffer_59 (buffer_59_out, buffer_60_out);
  buf buffer_60 (buffer_60_out, buffer_61_out);
  buf buffer_61 (buffer_61_out, buffer_62_out);
  buf buffer_62 (buffer_62_out, buffer_75_out);
  buf buffer_63 (buffer_63_out, buffer_50_out);
  buf buffer_64 (buffer_64_out, buffer_63_out);
  buf buffer_65 (buffer_65_out, buffer_64_out);
  buf buffer_66 (buffer_66_out, buffer_65_out);
  buf buffer_67 (buffer_67_out, buffer_68_out);
  buf buffer_68 (buffer_68_out, buffer_69_out);
  buf buffer_69 (buffer_69_out, buffer_70_out);
  buf buffer_70 (buffer_70_out, buffer_83_out);
  buf buffer_71 (buffer_71_out, buffer_58_out);
  buf buffer_72 (buffer_72_out, buffer_71_out);
  buf buffer_73 (buffer_73_out, buffer_72_out);
  buf buffer_74 (buffer_74_out, buffer_73_out);
  buf buffer_75 (buffer_75_out, buffer_76_out);
  buf buffer_76 (buffer_76_out, buffer_77_out);
  buf buffer_77 (buffer_77_out, buffer_78_out);
  buf buffer_78 (buffer_78_out, buffer_91_out);
  buf buffer_79 (buffer_79_out, buffer_66_out);
  buf buffer_80 (buffer_80_out, buffer_79_out);
  buf buffer_81 (buffer_81_out, buffer_80_out);
  buf buffer_82 (buffer_82_out, buffer_81_out);
  buf buffer_83 (buffer_83_out, buffer_84_out);
  buf buffer_84 (buffer_84_out, buffer_85_out);
  buf buffer_85 (buffer_85_out, buffer_86_out);
  buf buffer_86 (buffer_86_out, buffer_99_out);
  buf buffer_87 (buffer_87_out, buffer_74_out);
  buf buffer_88 (buffer_88_out, buffer_87_out);
  buf buffer_89 (buffer_89_out, buffer_88_out);
  buf buffer_90 (buffer_90_out, buffer_89_out);
  buf buffer_91 (buffer_91_out, buffer_92_out);
  buf buffer_92 (buffer_92_out, buffer_93_out);
  buf buffer_93 (buffer_93_out, buffer_94_out);
  buf buffer_94 (buffer_94_out, buffer_109_out);
  buf buffer_95 (buffer_95_out, buffer_82_out);
  buf buffer_96 (buffer_96_out, buffer_95_out);
  buf buffer_97 (buffer_97_out, buffer_96_out);
  buf buffer_98 (buffer_98_out, buffer_97_out);
  buf buffer_99 (buffer_99_out, buffer_100_out);
  buf buffer_100 (buffer_100_out, buffer_101_out);
  buf buffer_101 (buffer_101_out, buffer_102_out);
  buf buffer_102 (buffer_102_out, buffer_117_out);
  buf buffer_103 (buffer_103_out, buffer_106_out);
  buf buffer_104 (buffer_104_out, buffer_103_out);
  buf buffer_105 (buffer_105_out, buffer_90_out);
  buf buffer_106 (buffer_106_out, buffer_105_out);
  buf buffer_107 (buffer_107_out, buffer_108_out);
  buf buffer_108 (buffer_108_out, buffer_122_out);
  buf buffer_109 (buffer_109_out, buffer_110_out);
  buf buffer_110 (buffer_110_out, buffer_107_out);
  buf buffer_111 (buffer_111_out, buffer_114_out);
  buf buffer_112 (buffer_112_out, buffer_111_out);
  buf buffer_113 (buffer_113_out, buffer_98_out);
  buf buffer_114 (buffer_114_out, buffer_113_out);
  buf buffer_115 (buffer_115_out, buffer_116_out);
  buf buffer_116 (buffer_116_out, buffer_127_out);
  buf buffer_117 (buffer_117_out, buffer_118_out);
  buf buffer_118 (buffer_118_out, buffer_115_out);
  buf buffer_119 (buffer_119_out, buffer_104_out);
  buf buffer_120 (buffer_120_out, buffer_119_out);
  buf buffer_121 (buffer_121_out, buffer_120_out);
  buf buffer_122 (buffer_122_out, buffer_123_out);
  buf buffer_123 (buffer_123_out, buffer_121_out);
  buf buffer_124 (buffer_124_out, buffer_112_out);
  buf buffer_125 (buffer_125_out, buffer_124_out);
  buf buffer_126 (buffer_126_out, buffer_125_out);
  buf buffer_127 (buffer_127_out, buffer_128_out);
  buf buffer_128 (buffer_128_out, buffer_126_out);
endmodule

module sign_controller (
  input  [31:0] in_1,
  input  [31:0] in_2,
  output out_3,
  output [31:0] out_4,
  output [31:0] out_5
);

  wire not_1_out, not_2_out;
  wire [31:0] negator_1_out, negator_2_out;

  not not_1 (not_1_out, in_1[31]);
  Negator #(.width(32)) negator_1 (.in(in_1), .out(negator_1_out));
  not not_2 (not_2_out, in_2[31]);
  Negator #(.width(32)) negator_2 (.in(in_2), .out(negator_2_out));
  Multiplexer #(.width(32)) multiplexer_1 (.in0(negator_1_out), .in1(in_1), .out(out_4), .sel(not_1_out));
  Multiplexer #(.width(32)) multiplexer_2 (.in0(negator_2_out), .in1(in_2), .out(out_5), .sel(not_2_out));
  xnor xnor_1 (out_3, not_1_out, not_2_out);
endmodule
module FPU (
  input  [31:0] in_1,
  input  [31:0] in_2,
  input  [5:0] in_3,
  output out_4,
  output [31:0] out_5,
  output out_6,
  output out_7
);

  wire and_1_out, and_2_out, and_3_out, and_4_out, and_5_out, and_6_out, bitfinder_1_found,
       bitfinder_3_found, comparator_1_eq, comparator_1_lt, comparator_2_eq, comparator_2_gt,
       comparator_2_lt, comparator_3_eq, comparator_3_gt, comparator_3_lt, comparator_4_lt,
       controlled_buffer_4_out, decoder_1_out0, decoder_1_out1, decoder_1_out2, decoder_1_out3,
       decoder_1_out4, decoder_1_out5, decoder_1_out6, decoder_1_out7, decoder_1_out11, decoder_1_out12,
       decoder_1_out13, decoder_1_out15, multiplexer_20_out, multiplexer_21_out, multiplexer_22_out,
       multiplexer_23_out, nand_1_out, not_2_out, not_3_out, not_4_out, not_5_out, not_6_out, or_1_out,
       or_2_out, or_3_out, or_4_out, or_5_out, or_6_out, or_7_out, or_8_out, or_9_out, or_10_out,
       pull_resistor_3_node, subtractor_2_bout, subtractor_3_bout, subtractor_4_bout, subtractor_7_bout,
       xnor_1_out, xor_1_out, xor_3_out;
  wire [4:0] bit_extender_1_out, bit_extender_10_out, bitfinder_1_index, bitfinder_4_index,
       multiplexer_5_out, multiplexer_8_out, multiplexer_12_out, negator_2_out, negator_3_out, negator_6_out,
       subtractor_2_out, subtractor_3_out, subtractor_7_out;
  wire [7:0] adder_1_out, adder_2_out, adder_3_out, adder_6_out, bit_extender_2_out, bit_extender_11_out,
       controlled_buffer_1_out, multiplexer_1_out, multiplexer_2_out, multiplexer_6_out, multiplexer_7_out,
       multiplexer_9_out, multiplexer_10_out, multiplexer_11_out, multiplexer_16_out, multiplexer_18_out,
       negator_4_out, pull_resistor_1_node_3, subtractor_1_out, subtractor_4_out, subtractor_5_out;
  wire [22:0] adder_4_out, bit_extender_7_out, bit_extender_8_out, bit_extender_12_out,
       controlled_buffer_1_out_3, multiplexer_1_out_2, multiplexer_17_out, pull_resistor_1_node;
  wire [23:0] multiplier_1_cout, shifter_1_out;
  wire [23:23] bitfinder_2_found;
  wire [30:0] adder_5_out, bit_extender_5_out, bit_extender_6_out, multiplexer_14_out, multiplexer_15_out,
       multiplexer_25_out, multiplexer_26_out, multiplexer_27_out, multiplexer_30_out, shifter_4_out,
       shifter_7_out, shifter_8_out, subtractor_6_out;
  wire [31:0] bit_extender_9_out, controlled_buffer_5_out, fpadder_1_out, fpdivider_1_out,
       fpmultiplier_1_out, fpsubtractor_1_out, fptoint_1_p2, inttofp_1_p3, multiplexer_3_out,
       multiplexer_4_out, multiplexer_19_out, multiplexer_24_out, multiplexer_28_out, negator_1_out,
       negator_5_out, shifter_2_out, shifter_3_out, shifter_5_out, shifter_6_out;
  wire [31:31] controlled_buffer_1_out_2, multiplexer_1_out_3, multiplexer_13_out, not_1_out,
       pull_resistor_1_node_2, xor_2_out;
  wire [63:0] bit_extender_3_out, bit_extender_4_out, divider_1_out;

  assign {controlled_buffer_1_out_2[31], controlled_buffer_1_out, controlled_buffer_1_out_3} = in_3[5] ? in_1 : 32'bz;  // Controlled_Buffer controlled_buffer_1
  Pull_Resistor pull_resistor_1 (.node({pull_resistor_1_node_2[31], pull_resistor_1_node_3, pull_resistor_1_node}));
  assign {pull_resistor_1_node_2[31], pull_resistor_1_node_3, pull_resistor_1_node} = in_3[5] ? in_2 : 32'bz;  // Controlled_Buffer controlled_buffer_2
  Pull_Resistor pull_resistor_2 (.node({controlled_buffer_1_out_2[31], controlled_buffer_1_out, controlled_buffer_1_out_3}));
  Multiplexer #(.width(32)) multiplexer_1 (
    .in0({pull_resistor_1_node_2[31], pull_resistor_1_node_3, pull_resistor_1_node}), .in1(32'h3f800000),
    .out({multiplexer_1_out_3[31], multiplexer_1_out, multiplexer_1_out_2}), .sel(or_1_out));
  or or_1 (or_1_out, decoder_1_out11, decoder_1_out12);
  FPMultiplier fpmultiplier_1 (
    .a({controlled_buffer_1_out_2[31], controlled_buffer_1_out, controlled_buffer_1_out_3}),
    .b({pull_resistor_1_node_2[31], pull_resistor_1_node_3, pull_resistor_1_node}), .out(fpmultiplier_1_out));
  FPDivider fpdivider_1 (
    .a({controlled_buffer_1_out_2[31], controlled_buffer_1_out, controlled_buffer_1_out_3}),
    .b({pull_resistor_1_node_2[31], pull_resistor_1_node_3, pull_resistor_1_node}), .out(fpdivider_1_out));
  // FPComparator fpcomparator_1: pin names not known; wires that end beside it: {controlled_buffer_1_out_2[31], controlled_buffer_1_out, controlled_buffer_1_out_3}, {pull_resistor_1_node_2[31], pull_resistor_1_node_3, pull_resistor_1_node}, out_6, out_7, multiplier_1_cout[23]
  BitFinder #(.\type ("high1"), .width(32)) bitfinder_1 (
    .in(multiplexer_4_out), .index(bitfinder_1_index), .found(bitfinder_1_found));
  Negator #(.width(32)) negator_1 (
    .in({pull_resistor_1_node_2[31], pull_resistor_1_node_3, pull_resistor_1_node}), .out(negator_1_out));
  Subtractor subtractor_1 (.a(pull_resistor_1_node_3), .b(8'h7f), .out(subtractor_1_out));  // open: bin, bout
  not not_1 (not_1_out[31], pull_resistor_1_node_2[31]);
  Multiplexer #(.width(8)) multiplexer_2 (.in0(8'h1), .in1({8{1'b1}}), .out(multiplexer_2_out), .sel(decoder_1_out5));
  or or_2 (or_2_out, decoder_1_out1, decoder_1_out15, decoder_1_out12);
  Multiplexer #(.width(32)) multiplexer_3 (
    .in0(fpmultiplier_1_out), .in1(fpdivider_1_out), .out(multiplexer_3_out), .sel(decoder_1_out3));
  Subtractor #(.width(5)) subtractor_2 (
    .a(5'b10111), .b(bitfinder_1_index), .out(subtractor_2_out), .bout(subtractor_2_bout));  // open: bin
  Multiplexer #(.width(32)) multiplexer_4 (
    .in0({pull_resistor_1_node_2[31], pull_resistor_1_node_3, pull_resistor_1_node}), .in1(negator_1_out),
    .out(multiplexer_4_out), .sel(pull_resistor_1_node_2[31]));
  Bit_Extender #(.out_width(5), .\type ("zero")) bit_extender_1 (.in(subtractor_1_out), .out(bit_extender_1_out));
  Adder adder_1 (.a(pull_resistor_1_node_3), .b(multiplexer_2_out), .out(adder_1_out));  // open: cin, cout
  xor xor_1 (xor_1_out, or_2_out, multiplexer_1_out_3[31]);
  Comparator #(.width(32)) comparator_1 (
    .a({1'b0, controlled_buffer_1_out, controlled_buffer_1_out_3}),
    .b({1'b0, multiplexer_1_out, multiplexer_1_out_2}), .eq(comparator_1_eq), .lt(comparator_1_lt));  // open: gt
  xor xor_2 (xor_2_out[31], controlled_buffer_1_out_2[31], pull_resistor_1_node_2[31]);
  Multiplier #(.width(24)) multiplier_1 (
    .a({1'b1, controlled_buffer_1_out_3}), .b({1'b1, pull_resistor_1_node}), .cout(multiplier_1_cout));  // open: out, cin
  Multiplexer #(.width(5)) multiplexer_5 (
    .in0(5'b00001), .in1({5{1'b0}}), .out(multiplexer_5_out), .sel(multiplier_1_cout[23]));
  Multiplexer #(.width(8)) multiplexer_6 (
    .in0(controlled_buffer_1_out), .in1(subtractor_5_out), .out(multiplexer_6_out), .sel(decoder_1_out3));
  Multiplexer #(.width(8)) multiplexer_7 (
    .in0(adder_2_out), .in1(controlled_buffer_1_out), .out(multiplexer_7_out), .sel(decoder_1_out3));
  xnor xnor_1 (xnor_1_out, controlled_buffer_1_out_2[31], pull_resistor_1_node_2[31]);
  Comparator #(.mode("unsigned"), .width(23)) comparator_2 (
    .a(controlled_buffer_1_out_3), .b(pull_resistor_1_node), .gt(comparator_2_gt), .eq(comparator_2_eq),
    .lt(comparator_2_lt));
  Comparator comparator_3 (
    .a(controlled_buffer_1_out), .b(pull_resistor_1_node_3), .gt(comparator_3_gt), .eq(comparator_3_eq),
    .lt(comparator_3_lt));
  and and_1 (and_1_out, pull_resistor_1_node_2[31], ~controlled_buffer_1_out_2[31]);  // AND_Gate
  Multiplexer #(.width(5)) multiplexer_8 (
    .in0(subtractor_2_out), .in1(negator_2_out), .out(multiplexer_8_out), .sel(pull_resistor_3_node));
  Negator #(.width(5)) negator_2 (.in(subtractor_2_out), .out(negator_2_out));
  Pull_Resistor pull_resistor_3 (.node(pull_resistor_3_node));
  assign pull_resistor_3_node = bitfinder_1_found ? subtractor_2_bout : 1'bz;  // Controlled_Buffer controlled_buffer_3
  not not_2 (not_2_out, pull_resistor_3_node);
  assign bit_extender_2_out = {{3{1'b0}}, bitfinder_1_index};  // Bit_Extender bit_extender_2
  Subtractor #(.width(5)) subtractor_3 (
    .a(5'b10111), .b(bit_extender_1_out), .out(subtractor_3_out), .bout(subtractor_3_bout));  // open: bin
  assign controlled_buffer_4_out = bitfinder_2_found[23] ? subtractor_3_bout : 1'bz;  // Controlled_Buffer controlled_buffer_4
  BitFinder #(.\type ("high1"), .width(32)) bitfinder_2 (
    .in({pull_resistor_1_node_2[31], pull_resistor_1_node_3, pull_resistor_1_node}),
    .found(bitfinder_2_found[23]));  // open: index
  nand nand_1 (nand_1_out, comparator_1_eq, not_3_out);
  not not_3 (not_3_out, bitfinder_3_found);
  BitFinder #(.\type ("high1")) bitfinder_3 (.in(subtractor_4_out), .found(bitfinder_3_found));  // open: index
  Subtractor subtractor_4 (
    .a(controlled_buffer_1_out), .b(multiplexer_1_out), .out(subtractor_4_out), .bout(subtractor_4_bout));  // open: bin
  Multiplexer #(.width(8)) multiplexer_9 (
    .in0(controlled_buffer_1_out), .in1(multiplexer_1_out), .out(multiplexer_9_out), .sel(subtractor_4_bout));
  assign bit_extender_3_out = {{40{1'b0}}, {1'b1, controlled_buffer_1_out_3}};  // Bit_Extender bit_extender_3
  assign bit_extender_4_out = {{40{1'b0}}, {1'b1, pull_resistor_1_node}};  // Bit_Extender bit_extender_4
  Shifter #(.width(24)) shifter_1 (.in(multiplier_1_cout), .\dist (multiplexer_5_out), .out(shifter_1_out));
  or or_3 (or_3_out, multiplier_1_cout[23], decoder_1_out3);
  Multiplexer #(.width(8)) multiplexer_10 (
    .in0(pull_resistor_1_node_3), .in1(8'h7f), .out(multiplexer_10_out), .sel(decoder_1_out3));
  Adder adder_2 (.a(multiplexer_10_out), .b(multiplexer_6_out), .out(adder_2_out), .cin(or_3_out));  // open: cout
  Subtractor subtractor_5 (
    .a(multiplexer_7_out), .b(multiplexer_11_out), .out(subtractor_5_out), .bin(decoder_1_out3));  // open: bout
  Multiplexer #(.width(8)) multiplexer_11 (
    .in0(8'h7f), .in1(pull_resistor_1_node_3), .out(multiplexer_11_out), .sel(decoder_1_out3));
  and and_2 (and_2_out, comparator_2_gt, comparator_3_eq);
  and and_3 (and_3_out, comparator_2_lt, comparator_3_eq);
  and and_4 (and_4_out, ~pull_resistor_1_node_2[31], controlled_buffer_1_out_2[31]);  // AND_Gate
  Shifter #(.shift("lr"), .width(32)) shifter_2 (
    .in(multiplexer_4_out), .\dist (multiplexer_8_out), .out(shifter_2_out));
  Shifter #(.width(32)) shifter_3 (.in(multiplexer_4_out), .\dist (multiplexer_8_out), .out(shifter_3_out));
  Adder adder_3 (.a(8'h7f), .b(bit_extender_2_out), .out(adder_3_out));  // open: cin, cout
  Multiplexer #(.width(5)) multiplexer_12 (
    .in0(subtractor_3_out), .in1(negator_3_out), .out(multiplexer_12_out), .sel(controlled_buffer_4_out));
  Negator #(.width(5)) negator_3 (.in(subtractor_3_out), .out(negator_3_out));
  Multiplexer multiplexer_13 (
    .in0(controlled_buffer_1_out_2[31]), .in1(xor_1_out), .out(multiplexer_13_out[31]), .sel(comparator_1_lt));
  xor xor_3 (xor_3_out, controlled_buffer_1_out_2[31], xor_1_out);
  Multiplexer #(.width(31)) multiplexer_14 (
    .in0(bit_extender_5_out), .in1(bit_extender_6_out), .out(multiplexer_14_out), .sel(subtractor_4_bout));
  Multiplexer #(.width(31)) multiplexer_15 (
    .in0(bit_extender_6_out), .in1(bit_extender_5_out), .out(multiplexer_15_out), .sel(subtractor_4_bout));
  assign bit_extender_5_out = {{7{1'b0}}, {1'b1, controlled_buffer_1_out_3}};  // Bit_Extender bit_extender_5
  assign bit_extender_6_out = {{7{1'b0}}, {1'b1, multiplexer_1_out_2}};  // Bit_Extender bit_extender_6
  Multiplexer #(.width(8)) multiplexer_16 (
    .in0(subtractor_4_out), .in1(negator_4_out), .out(multiplexer_16_out), .sel(subtractor_4_bout));
  Negator negator_4 (.in(subtractor_4_out), .out(negator_4_out));
  Divider #(.width(64)) divider_1 (
    .a({64{1'b0}}), .b(bit_extender_4_out), .out(divider_1_out), .upper(bit_extender_3_out));  // open: rem
  Multiplexer #(.width(23)) multiplexer_17 (
    .in0(adder_4_out), .in1(bit_extender_7_out), .out(multiplexer_17_out), .sel(not_4_out));
  Bit_Extender #(.in_width(24), .out_width(23), .\type ("zero")) bit_extender_7 (
    .in(shifter_1_out), .out(bit_extender_7_out));
  not not_4 (not_4_out, decoder_1_out3);
  Multiplexer #(.width(8)) multiplexer_18 (
    .in0(adder_2_out), .in1(subtractor_5_out), .out(multiplexer_18_out), .sel(not_4_out));
  or or_4 (or_4_out, comparator_3_gt, and_2_out);
  not not_5 (not_5_out, xnor_1_out);
  and and_5 (and_5_out, comparator_2_eq, xnor_1_out, comparator_3_eq);
  or or_5 (or_5_out, and_3_out, comparator_3_lt);
  Bit_Extender #(.in_width(32), .out_width(23), .\type ("zero")) bit_extender_8 (
    .in(multiplexer_19_out), .out(bit_extender_8_out));
  Multiplexer #(.width(32)) multiplexer_19 (
    .in0(shifter_2_out), .in1(shifter_3_out), .out(multiplexer_19_out), .sel(not_2_out));
  assign bit_extender_9_out = {{8{1'b0}}, {bitfinder_2_found[23], pull_resistor_1_node}};  // Bit_Extender bit_extender_9
  Pull_Resistor pull_resistor_4 (.node(controlled_buffer_4_out));
  FPAdder fpadder_1 (
    .a({controlled_buffer_1_out_2[31], controlled_buffer_1_out, controlled_buffer_1_out_3}),
    .b({multiplexer_1_out_3[31], multiplexer_1_out, multiplexer_1_out_2}), .out(fpadder_1_out));
  FPSubtractor fpsubtractor_1 (
    .a({controlled_buffer_1_out_2[31], controlled_buffer_1_out, controlled_buffer_1_out_3}),
    .b({multiplexer_1_out_3[31], multiplexer_1_out, multiplexer_1_out_2}), .out(fpsubtractor_1_out));
  not not_6 (not_6_out, xor_3_out);
  Comparator #(.width(31)) comparator_4 (
    .a(multiplexer_14_out), .b(shifter_4_out), .lt(comparator_4_lt));  // open: gt, eq
  Shifter #(.shift("lr"), .width(31)) shifter_4 (
    .in(multiplexer_15_out), .\dist (bit_extender_10_out), .out(shifter_4_out));
  Bit_Extender #(.out_width(5), .\type ("zero")) bit_extender_10 (.in(multiplexer_16_out), .out(bit_extender_10_out));
  assign bit_extender_11_out = {{3{subtractor_7_out[4]}}, subtractor_7_out};  // Bit_Extender bit_extender_11
  Multiplexer multiplexer_20 (.in0(or_4_out), .in1(and_1_out), .out(multiplexer_20_out), .sel(not_5_out));
  Multiplexer multiplexer_21 (
    .in0(multiplexer_20_out), .in1(multiplexer_22_out), .out(multiplexer_21_out), .sel(and_6_out));
  Multiplexer multiplexer_22 (.in0(or_5_out), .in1(and_4_out), .out(multiplexer_22_out), .sel(not_5_out));
  Multiplexer multiplexer_23 (
    .in0(multiplexer_22_out), .in1(multiplexer_20_out), .out(multiplexer_23_out), .sel(and_6_out));
  and and_6 (and_6_out, pull_resistor_1_node_2[31], controlled_buffer_1_out_2[31]);
  assign controlled_buffer_5_out = bitfinder_1_found ? {pull_resistor_1_node_2[31], adder_3_out, bit_extender_8_out} : 32'bz;  // Controlled_Buffer controlled_buffer_5
  Shifter #(.shift("lr"), .width(32)) shifter_5 (
    .in(bit_extender_9_out), .\dist (multiplexer_12_out), .out(shifter_5_out));
  Shifter #(.width(32)) shifter_6 (.in(bit_extender_9_out), .\dist (multiplexer_12_out), .out(shifter_6_out));
  Multiplexer #(.width(32)) multiplexer_24 (
    .in0(fpadder_1_out), .in1(fpsubtractor_1_out), .out(multiplexer_24_out), .sel(or_2_out));
  Multiplexer #(.width(31)) multiplexer_25 (
    .in0(multiplexer_14_out), .in1(shifter_4_out), .out(multiplexer_25_out), .sel(comparator_4_lt));
  Multiplexer #(.width(31)) multiplexer_26 (
    .in0(shifter_4_out), .in1(multiplexer_14_out), .out(multiplexer_26_out), .sel(comparator_4_lt));
  BitFinder #(.\type ("high1"), .width(31)) bitfinder_4 (
    .in(multiplexer_30_out), .index(bitfinder_4_index));  // open: found
  Multiplexer #(.width(31)) multiplexer_27 (
    .in0(shifter_7_out), .in1(shifter_8_out), .out(multiplexer_27_out), .sel(subtractor_7_bout));
  or or_6 (or_6_out, divider_1_out[39], divider_1_out[40]);
  Adder #(.width(23)) adder_4 (
    .a(divider_1_out[63:41]), .b({23{1'b0}}), .out(adder_4_out), .cin(or_6_out));  // open: cout
  or or_7 (or_7_out, or_8_out, decoder_1_out5);
  or or_8 (or_8_out, decoder_1_out0, decoder_1_out1);
  or or_9 (or_9_out, decoder_1_out2, decoder_1_out3);
  Decoder #(.select(4)) decoder_1 (
    .out0(decoder_1_out0), .out1(decoder_1_out1), .out2(decoder_1_out2), .out3(decoder_1_out3),
    .out4(decoder_1_out4), .out5(decoder_1_out5), .out6(decoder_1_out6), .out7(decoder_1_out7),
    .out11(decoder_1_out11), .out12(decoder_1_out12), .out13(decoder_1_out13), .out15(decoder_1_out15),
    .sel(in_3[3:0]), .en(in_3[4]));  // open: out8, out9, out10, out14
  // IntToFP #(.width(32)) inttofp_1: pin names not known; wires that end beside it: {pull_resistor_1_node_2[31], pull_resistor_1_node_3, pull_resistor_1_node}, controlled_buffer_5_out, inttofp_1_p3
  // FPToInt #(.mode("truncate"), .width(32)) fptoint_1: pin names not known; wires that end beside it: {pull_resistor_1_node_2[31], pull_resistor_1_node_3, pull_resistor_1_node}, fptoint_1_p2, decoder_1_out6, out_4
  Multiplexer #(.width(32)) multiplexer_28 (
    .in0(shifter_5_out), .in1(shifter_6_out), .out(multiplexer_28_out), .sel(controlled_buffer_4_out));
  Negator #(.width(32)) negator_5 (.in(multiplexer_28_out), .out(negator_5_out));
  Subtractor #(.width(31)) subtractor_6 (
    .a(multiplexer_25_out), .b(multiplexer_26_out), .out(subtractor_6_out));  // open: bin, bout
  Adder #(.width(31)) adder_5 (.a(multiplexer_25_out), .b(multiplexer_26_out), .out(adder_5_out));  // open: cin, cout
  Subtractor #(.width(5)) subtractor_7 (
    .a(bitfinder_4_index), .b(5'b10111), .out(subtractor_7_out), .bout(subtractor_7_bout));  // open: bin
  Negator #(.width(5)) negator_6 (.in(subtractor_7_out), .out(negator_6_out));
  Bit_Extender #(.in_width(31), .out_width(23), .\type ("zero")) bit_extender_12 (
    .in(multiplexer_27_out), .out(bit_extender_12_out));
  Adder adder_6 (.a(bit_extender_11_out), .b(multiplexer_9_out), .out(adder_6_out));  // open: cin, cout
  or or_10 (or_10_out, decoder_1_out4, decoder_1_out5);
  or or_11 (decoder_1_out5, decoder_1_out11, decoder_1_out12);
  Multiplexer #(.width(32)) multiplexer_29 (
    .in0(multiplexer_28_out), .in1(negator_5_out), .sel(pull_resistor_1_node_2[31]));  // open: out
  Multiplexer #(.width(31)) multiplexer_30 (
    .in0(subtractor_6_out), .in1(adder_5_out), .out(multiplexer_30_out), .sel(not_6_out));
  Shifter #(.shift("lr"), .width(31)) shifter_7 (
    .in(multiplexer_30_out), .\dist (subtractor_7_out), .out(shifter_7_out));
  Shifter #(.width(31)) shifter_8 (.in(multiplexer_30_out), .\dist (negator_6_out), .out(shifter_8_out));
  Controlled_Buffer #(.width(32)) controlled_buffer_6 (
    .in({multiplexer_13_out[31], adder_6_out, bit_extender_12_out}), .en(nand_1_out));  // open: out
  assign out_5 = decoder_1_out6 ? inttofp_1_p3 : 32'bz;  // Controlled_Buffer controlled_buffer_7
  assign out_5 = decoder_1_out7 ? fptoint_1_p2 : 32'bz;  // Controlled_Buffer controlled_buffer_8
  assign out_5 = decoder_1_out13 ? {not_1_out[31], pull_resistor_1_node_3, pull_resistor_1_node} : 32'bz;  // Controlled_Buffer controlled_buffer_9
  assign out_5 = or_10_out ? {pull_resistor_1_node_2[31], adder_1_out, pull_resistor_1_node} : 32'bz;  // Controlled_Buffer controlled_buffer_10
  assign out_5 = or_7_out ? multiplexer_24_out : 32'bz;  // Controlled_Buffer controlled_buffer_11
  assign out_5 = or_9_out ? multiplexer_3_out : 32'bz;  // Controlled_Buffer controlled_buffer_12
  Pull_Resistor pull_resistor_5 (.node(out_4));

  // Notes on the sheet:
  //   INT TO FLOAT
  //   FLOAT TO INT
  //   SHIFT
  //   0-LEFT
  //   1-RIGHT
  //   0-ADD
  //   1-SUB
  //   NEGATE
  //   0-MULT
  //   1-DIV
  //   COMP
endmodule
